// Logisim project CRC校验(P0.Q1).circ as structural Verilog: 3 circuits, main circuit CRC
module CRC (
  input  [7:0] A_8bit,
  input  [3:0] B_4bit,
  output [10:0] C_11bit
);

  wire [2:0] remainder1, remainder2, remainder3, remainder4, remainder5, remainder6, remainder7;
  wire [10:0] bit_extender_1_out, Dividend_10_0;

  // Probe on Dividend_10_0[10:7]
  \四位模二除法器  \u_四位模二除法器_1  (.A_4bit(Dividend_10_0[10:7]), .B_4bit(B_4bit), .C_3bit(remainder1));
  // Probe on remainder1
  // Probe on remainder3
  \四位模二除法器  \u_四位模二除法器_2  (.A_4bit({remainder2, Dividend_10_0[5]}), .B_4bit(B_4bit), .C_3bit(remainder3));
  // Probe on remainder5
  \四位模二除法器  \u_四位模二除法器_3  (.A_4bit({remainder4, Dividend_10_0[3]}), .B_4bit(B_4bit), .C_3bit(remainder5));
  // Probe on remainder7
  \四位模二除法器  \u_四位模二除法器_4  (.A_4bit({remainder6, Dividend_10_0[1]}), .B_4bit(B_4bit), .C_3bit(remainder7));
  assign bit_extender_1_out = {{3{1'b0}}, A_8bit};  // Bit_Extender bit_extender_1
  Shifter #(.width(11)) shifter_1 (.in(bit_extender_1_out), .\dist (4'b0011), .out(Dividend_10_0));
  // Probe on Dividend_10_0
  \四位模二除法器  \u_四位模二除法器_5  (.A_4bit({remainder1, Dividend_10_0[6]}), .B_4bit(B_4bit), .C_3bit(remainder2));
  \四位模二除法器  \u_四位模二除法器_6  (.A_4bit({remainder3, Dividend_10_0[4]}), .B_4bit(B_4bit), .C_3bit(remainder4));
  \四位模二除法器  \u_四位模二除法器_7  (.A_4bit({remainder5, Dividend_10_0[2]}), .B_4bit(B_4bit), .C_3bit(remainder6));
  \四位模二除法器  \u_四位模二除法器_8  (.A_4bit({remainder7, Dividend_10_0[0]}), .B_4bit(B_4bit), .C_3bit(C_11bit[2:0]));
  // Probe on remainder2
  // Probe on remainder4
  // Probe on remainder6
  // Probe on C_11bit[2:0]

  assign C_11bit[10:3] = A_8bit;

  // Other names for the same wires on the sheet: remainder_final[2:0] = C_11bit[2:0]; divisor[3:0] = B_4bit
endmodule

module \四位模二除法器  (
  input  [3:0] A_4bit,
  input  [3:0] B_4bit,
  output [2:0] C_3bit
);

  \四位模二除法器实现  \u_四位模二除法器实现_1  (
    .A0(A_4bit[0]), .C0(C_3bit[0]), .A1(A_4bit[1]), .A2(A_4bit[2]), .B0(B_4bit[0]), .C1(C_3bit[1]),
    .B1(B_4bit[1]), .B2(B_4bit[2]), .C2(C_3bit[2]), .msb(A_4bit[3]));
endmodule

module \四位模二除法器实现  (
  input  A0,
  input  A1,
  input  A2,
  input  B0,
  input  B1,
  input  B2,
  input  msb,
  output C0,
  output C1,
  output C2
);

  wire and_1_out, and_2_out, and_3_out, and_4_out, and_5_out, and_6_out, not_1_out, not_2_out, not_3_out,
       xor_1_out, xor_2_out, xor_3_out;

  and and_1 (and_1_out, msb, xor_1_out);
  xor xor_1 (xor_1_out, A0, B0);
  not not_1 (not_1_out, msb);
  and and_2 (and_2_out, not_1_out, A0);
  and and_3 (and_3_out, msb, xor_2_out);
  xor xor_2 (xor_2_out, A1, B1);
  not not_2 (not_2_out, msb);
  and and_4 (and_4_out, not_2_out, A1);
  and and_5 (and_5_out, msb, xor_3_out);
  xor xor_3 (xor_3_out, A2, B2);
  not not_3 (not_3_out, msb);
  and and_6 (and_6_out, not_3_out, A2);
  or or_1 (C0, and_1_out, and_2_out);
  or or_2 (C1, and_3_out, and_4_out);
  or or_3 (C2, and_5_out, and_6_out);
endmodule
