// Logisim project Logisim中的FSM(P0.Q4) - 副本.circ as structural Verilog: 4 circuits, main circuit fsm
module fsm (
  input  CLR,
  input  [1:0] IN_1_0,
  output Z
);

  wire \状态存储_1_out_4 , \状态存储_1_out_5 , \状态存储_1_out_6 , \状态转移_1_s0_new , \状态转移_1_s1_new , \状态转移_1_s2_new ;

  Clock clock_1 ();  // open: out
  \状态转移  \u_状态转移_1  (
    .CLR(CLR), .S2(\状态存储_1_out_4 ), .S1(\状态存储_1_out_5 ), .S0(\状态存储_1_out_6 ), .IN1(IN_1_0[1]),
    .IN0(IN_1_0[0]), .S2_NEW(\状态转移_1_s2_new ), .S1_NEW(\状态转移_1_s1_new ), .S0_NEW(\状态转移_1_s0_new ));
  \状态存储  \u_状态存储_1  (
    .S2_prime(\状态转移_1_s2_new ), .S1_prime(\状态转移_1_s1_new ), .S0_prime(\状态转移_1_s0_new ),
    .out_4(\状态存储_1_out_4 ), .out_5(\状态存储_1_out_5 ), .out_6(\状态存储_1_out_6 ));
  \状态输出  \u_状态输出_1  (
    .S2(\状态存储_1_out_4 ), .S1(\状态存储_1_out_5 ), .S0(\状态存储_1_out_6 ), .IN1(IN_1_0[1]), .IN0(IN_1_0[0]),
    .S2_NEW(Z));
endmodule

module \状态转移  (
  input  CLR,
  input  S2,
  input  S1,
  input  S0,
  input  IN1,
  input  IN0,
  output S2_NEW,
  output S1_NEW,
  output S0_NEW
);

  wire and_1_out, and_2_out, and_3_out, and_4_out, and_5_out, and_6_out, and_7_out, and_8_out, not_1_out,
       not_2_out, not_3_out, not_4_out, not_5_out, not_6_out, not_7_out, not_8_out, not_9_out, not_10_out,
       not_11_out, not_12_out, not_13_out, not_14_out, not_15_out, not_16_out, not_17_out, not_18_out,
       not_19_out, not_20_out, not_21_out, not_22_out, not_23_out;

  not not_1 (not_1_out, CLR);
  not not_2 (not_2_out, IN0);
  not not_3 (not_3_out, CLR);
  not not_4 (not_4_out, S1);
  not not_5 (not_5_out, IN1);
  not not_6 (not_6_out, CLR);
  not not_7 (not_7_out, S1);
  not not_8 (not_8_out, IN0);
  not not_9 (not_9_out, CLR);
  not not_10 (not_10_out, S0);
  not not_11 (not_11_out, IN0);
  not not_12 (not_12_out, CLR);
  not not_13 (not_13_out, S1);
  not not_14 (not_14_out, S0);
  not not_15 (not_15_out, IN1);
  not not_16 (not_16_out, CLR);
  not not_17 (not_17_out, S1);
  not not_18 (not_18_out, IN1);
  not not_19 (not_19_out, IN0);
  not not_20 (not_20_out, CLR);
  not not_21 (not_21_out, S0);
  not not_22 (not_22_out, IN1);
  not not_23 (not_23_out, IN0);
  and and_1 (and_1_out, not_1_out, S1, S0, not_2_out);
  and and_2 (and_2_out, S2, S0);
  and and_3 (and_3_out, not_3_out, not_4_out, S0, not_5_out);
  and and_4 (and_4_out, not_6_out, not_7_out, S0, not_8_out);
  and and_5 (and_5_out, not_9_out, S1, not_10_out, not_11_out);
  and and_6 (and_6_out, not_12_out, not_13_out, not_14_out, not_15_out, IN0);
  and and_7 (and_7_out, not_16_out, not_17_out, S0, not_18_out, not_19_out);
  and and_8 (and_8_out, not_20_out, S1, not_21_out, not_22_out, not_23_out);
  or or_1 (S2_NEW, and_1_out, and_2_out);
  or or_2 (S1_NEW, and_3_out, and_4_out, and_5_out);
  or or_3 (S0_NEW, and_6_out, and_7_out, and_8_out);
endmodule

module \状态存储  (
  input  S2_prime,
  input  S1_prime,
  input  S0_prime,
  output out_4,
  output out_5,
  output out_6
);

  wire clock_1_out;

  Register #(.width(1)) register_1 (.D(S2_prime), .Q(out_4), .clk(clock_1_out));  // open: en, clr
  Register #(.width(1)) register_2 (.D(S1_prime), .Q(out_5), .clk(clock_1_out));  // open: en, clr
  Register #(.width(1)) register_3 (.D(S0_prime), .Q(out_6), .clk(clock_1_out));  // open: en, clr
  Clock clock_1 (.out(clock_1_out));
endmodule

module \状态输出  (
  input  S2,
  input  S1,
  input  S0,
  input  IN1,
  input  IN0,
  output S2_NEW
);

  wire and_1_out, and_2_out, and_3_out, and_4_out, and_5_out, and_6_out, and_7_out, and_8_out, not_1_out,
       not_2_out, not_3_out, not_4_out, not_5_out, not_6_out, not_7_out, not_8_out, not_9_out, not_10_out,
       not_11_out, not_12_out, not_13_out, not_14_out, not_15_out, not_16_out;

  not not_1 (not_1_out, IN0);
  not not_2 (not_2_out, S1);
  not not_3 (not_3_out, IN1);
  not not_4 (not_4_out, S1);
  not not_5 (not_5_out, IN0);
  not not_6 (not_6_out, S0);
  not not_7 (not_7_out, IN0);
  not not_8 (not_8_out, S1);
  not not_9 (not_9_out, S0);
  not not_10 (not_10_out, IN1);
  not not_11 (not_11_out, S1);
  not not_12 (not_12_out, IN1);
  not not_13 (not_13_out, IN0);
  not not_14 (not_14_out, S0);
  not not_15 (not_15_out, IN1);
  not not_16 (not_16_out, IN0);
  and and_1 (and_1_out, S1, S0, not_1_out);
  and and_2 (and_2_out, S2, S0);
  and and_3 (and_3_out, not_2_out, S0, not_3_out);
  and and_4 (and_4_out, not_4_out, S0, not_5_out);
  and and_5 (and_5_out, S1, not_6_out, not_7_out);
  and and_6 (and_6_out, not_8_out, not_9_out, not_10_out, IN0);
  and and_7 (and_7_out, not_11_out, S0, not_12_out, not_13_out);
  and and_8 (and_8_out, S1, not_14_out, not_15_out, not_16_out);
  or or_1 (S2_NEW, and_1_out, and_2_out);
  // OR_Gate or_2 has open pins: in0=and_3_out, in1=and_4_out, in2=and_5_out, out=open
  // OR_Gate or_3 has open pins: in0=and_6_out, in1=and_7_out, in2=and_8_out, out=open
endmodule
