// Logisim project Logisim中的FSM(P0.Q4).circ as structural Verilog: 4 circuits, main circuit fsm
module fsm (
  input  CLR,
  input  [1:0] IN_1_0,
  output Z
);

  wire clock_1_out, \状态存储_1_out_6 , \状态存储_1_out_7 , \状态存储_1_out_8 , \状态转移_1_s0_new , \状态转移_1_s1_new ,
       \状态转移_1_s2_new ;

  \状态转移  \u_状态转移_1  (
    .S2(\状态存储_1_out_6 ), .S2_NEW(\状态转移_1_s2_new ), .S1(\状态存储_1_out_7 ), .S0(\状态存储_1_out_8 ), .IN1(IN_1_0[1]),
    .IN0(IN_1_0[0]), .S1_NEW(\状态转移_1_s1_new ), .S0_NEW(\状态转移_1_s0_new ));
  Clock clock_1 (.out(clock_1_out));
  \状态存储  \u_状态存储_1  (
    .S2_prime(\状态转移_1_s2_new ), .S1_prime(\状态转移_1_s1_new ), .S0_prime(\状态转移_1_s0_new ),
    .out_6(\状态存储_1_out_6 ), .out_7(\状态存储_1_out_7 ), .out_8(\状态存储_1_out_8 ), .CLR(CLR), .CLK(clock_1_out));
  \状态输出  \u_状态输出_1  (
    .S2(\状态存储_1_out_6 ), .S2_NEW(Z), .S1(\状态存储_1_out_7 ), .S0(\状态存储_1_out_8 ), .IN1(IN_1_0[1]),
    .IN0(IN_1_0[0]));
endmodule

module \状态转移  (
  input  S2,
  input  S1,
  input  S0,
  input  IN1,
  input  IN0,
  output S2_NEW,
  output S1_NEW,
  output S0_NEW
);

  wire and_1_out, and_2_out, and_3_out, and_4_out, and_5_out, and_6_out, and_7_out, and_8_out, and_9_out,
       and_10_out, not_1_out, not_2_out, not_3_out, not_4_out, not_5_out, not_6_out, not_7_out, not_8_out,
       not_9_out, not_10_out, not_11_out, not_12_out, not_13_out, not_14_out;

  not not_1 (not_1_out, IN0);
  not not_2 (not_2_out, S1);
  not not_3 (not_3_out, IN1);
  not not_4 (not_4_out, S1);
  not not_5 (not_5_out, IN0);
  not not_6 (not_6_out, S0);
  not not_7 (not_7_out, IN0);
  not not_8 (not_8_out, S1);
  not not_9 (not_9_out, S0);
  not not_10 (not_10_out, IN1);
  not not_11 (not_11_out, S1);
  not not_12 (not_12_out, IN0);
  not not_13 (not_13_out, S0);
  not not_14 (not_14_out, IN0);
  and and_1 (and_1_out, S1, S0, not_1_out);
  and and_2 (and_2_out, S2, S1);
  and and_3 (and_3_out, not_2_out, S0, not_3_out);
  and and_4 (and_4_out, not_4_out, S0, not_5_out);
  and and_5 (and_5_out, S1, not_6_out, not_7_out);
  and and_6 (and_6_out, S2, S1);
  and and_7 (and_7_out, not_8_out, not_9_out, not_10_out, IN0);
  and and_8 (and_8_out, not_11_out, S0, not_12_out);
  and and_9 (and_9_out, S1, not_13_out, not_14_out);
  and and_10 (and_10_out, S2, S1);
  or or_1 (S2_NEW, and_1_out, and_2_out);
  or or_2 (S1_NEW, and_3_out, and_4_out, and_5_out, and_6_out);
  or or_3 (S0_NEW, and_7_out, and_8_out, and_9_out, and_10_out);
endmodule

module \状态存储  (
  input  CLR,
  input  S2_prime,
  input  S1_prime,
  input  S0_prime,
  input  CLK,
  output out_6,
  output out_7,
  output out_8
);

  wire and_1_out, and_2_out, and_3_out, not_1_out;

  not not_1 (not_1_out, CLR);
  and and_1 (and_1_out, S2_prime, not_1_out);
  Register #(.width(1)) register_1 (.D(and_1_out), .Q(out_6), .clk(CLK));  // open: en, clr
  Register #(.width(1)) register_2 (.D(and_2_out), .Q(out_7), .clk(CLK));  // open: en, clr
  and and_2 (and_2_out, S1_prime, not_1_out);
  Register #(.width(1)) register_3 (.D(and_3_out), .Q(out_8), .clk(CLK));  // open: en, clr
  and and_3 (and_3_out, S0_prime, not_1_out);
endmodule

module \状态输出  (
  input  S2,
  input  S1,
  input  S0,
  input  IN1,
  input  IN0,
  output S2_NEW
);

  wire and_1_out, and_2_out, not_1_out;

  not not_1 (not_1_out, IN0);
  and and_1 (and_1_out, S1, S0, not_1_out);
  and and_2 (and_2_out, S2, S1);
  or or_1 (S2_NEW, and_1_out, and_2_out);
endmodule
