// Logisim project Logisim导航(P0.Q3).circ as structural Verilog: 5 circuits, main circuit navigation
module navigation (
  input  [1:0] dir_1_0,
  input  clk,
  input  reset,
  output arrive,
  output hit
);

  wire state_store_1_s0_old, state_store_1_s1_old, state_store_1_s2_old, state_trans_1_s0_new,
       state_trans_1_s1_new, state_trans_1_s2_new;

  state_trans state_trans_1 (
    .s2(state_store_1_s2_old), .s1(state_store_1_s1_old), .s0(state_store_1_s0_old), .d1(dir_1_0[1]),
    .d0(dir_1_0[0]), .s2_new(state_trans_1_s2_new), .s1_new(state_trans_1_s1_new),
    .s0_new(state_trans_1_s0_new));
  state_store state_store_1 (
    .s2new(state_trans_1_s2_new), .s1new(state_trans_1_s1_new), .s0new(state_trans_1_s0_new),
    .s2_old(state_store_1_s2_old), .s1_old(state_store_1_s1_old), .s0_old(state_store_1_s0_old), .CLK(clk),
    .RESET(reset));
  for_arrive for_arrive_1 (
    .s2_prime(state_trans_1_s2_new), .s1_prime(state_trans_1_s1_new), .s0_prime(state_trans_1_s0_new),
    .clk(clk), .reset(reset), .out_6(arrive));
  state_out state_out_1 (
    .s2(state_store_1_s2_old), .s1(state_store_1_s1_old), .s0(state_store_1_s0_old), .d1(dir_1_0[1]),
    .d0(dir_1_0[0]), .hit(hit), .clk(clk), .reset(reset));

  // Other names for the same wires on the sheet: clock = clk; d0 = dir_1_0[0]; d1 = dir_1_0[1]
endmodule

module state_trans (
  input  s2,
  input  s1,
  input  s0,
  input  d1,
  input  d0,
  output s2_new,
  output s1_new,
  output s0_new
);

  wire and_1_out, and_2_out, and_3_out, and_4_out, and_5_out, and_6_out, and_7_out, and_8_out, and_9_out,
       and_10_out, and_11_out, and_12_out, not_1_out, not_2_out, not_3_out, not_4_out, not_5_out, not_6_out,
       not_7_out, not_8_out, not_9_out, not_10_out, not_11_out, not_12_out, not_13_out, not_14_out,
       not_15_out, not_16_out, not_17_out;

  not not_1 (not_1_out, s0);
  not not_2 (not_2_out, d1);
  not not_3 (not_3_out, d0);
  not not_4 (not_4_out, d1);
  not not_5 (not_5_out, s1);
  not not_6 (not_6_out, d1);
  not not_7 (not_7_out, d1);
  not not_8 (not_8_out, d0);
  not not_9 (not_9_out, s0);
  not not_10 (not_10_out, d1);
  not not_11 (not_11_out, s0);
  not not_12 (not_12_out, d0);
  not not_13 (not_13_out, s2);
  not not_14 (not_14_out, s1);
  not not_15 (not_15_out, d1);
  not not_16 (not_16_out, d0);
  not not_17 (not_17_out, d0);
  and and_1 (and_1_out, s1, not_1_out, not_2_out, not_3_out);
  and and_2 (and_2_out, s1, s0, not_4_out, d0);
  and and_3 (and_3_out, s2, s0);
  and and_4 (and_4_out, not_5_out, s0, not_6_out);
  and and_5 (and_5_out, s0, not_7_out, not_8_out);
  and and_6 (and_6_out, s1, not_9_out, not_10_out, d0);
  and and_7 (and_7_out, s1, not_11_out, d1, not_12_out);
  and and_8 (and_8_out, s1, s0, d1, d0);
  and and_9 (and_9_out, not_13_out, not_14_out, not_15_out, not_16_out);
  and and_10 (and_10_out, s0, d1, d0);
  and and_11 (and_11_out, s1, d1, d0);
  and and_12 (and_12_out, s1, s0, not_17_out);
  or or_1 (s2_new, and_1_out, and_2_out, and_3_out);
  or or_2 (s1_new, and_4_out, and_5_out, and_6_out, and_7_out, and_8_out);
  or or_3 (s0_new, and_9_out, and_10_out, and_11_out, and_12_out);
endmodule

module state_store (
  input  CLK,
  input  s2new,
  input  s1new,
  input  s0new,
  input  RESET,
  output s2_old,
  output s1_old,
  output s0_old
);

  Register #(.width(1)) register_1 (.D(s2new), .Q(s2_old), .clk(CLK), .clr(RESET));  // open: en
  Register #(.width(1)) register_2 (.D(s1new), .Q(s1_old), .clk(CLK), .clr(RESET));  // open: en
  Register #(.width(1)) register_3 (.D(s0new), .Q(s0_old), .clk(CLK), .clr(RESET));  // open: en
endmodule

module state_out (
  input  s2,
  input  s1,
  input  s0,
  input  d1,
  input  d0,
  input  clk,
  input  reset,
  output hit
);

  wire and_1_out, and_2_out, and_3_out, and_4_out, and_5_out, not_1_out, not_2_out, not_3_out, not_4_out,
       not_5_out, not_6_out, not_7_out, not_8_out, not_9_out, not_10_out, not_11_out, not_12_out, or_1_out;

  not not_1 (not_1_out, s2);
  not not_2 (not_2_out, s0);
  not not_3 (not_3_out, d1);
  not not_4 (not_4_out, s2);
  not not_5 (not_5_out, s0);
  not not_6 (not_6_out, d0);
  not not_7 (not_7_out, s2);
  not not_8 (not_8_out, s1);
  not not_9 (not_9_out, s2);
  not not_10 (not_10_out, s2);
  not not_11 (not_11_out, d1);
  not not_12 (not_12_out, d0);
  and and_1 (and_1_out, not_1_out, not_2_out, not_3_out, d0);
  and and_2 (and_2_out, not_4_out, not_5_out, d1, not_6_out);
  and and_3 (and_3_out, not_7_out, not_8_out, d1, d0);
  and and_4 (and_4_out, not_9_out, s0, d1, d0);
  and and_5 (and_5_out, not_10_out, s1, s0, not_11_out, not_12_out);
  Register #(.width(1)) register_1 (.D(or_1_out), .Q(hit), .clk(clk), .clr(reset));  // open: en
  or or_1 (or_1_out, and_1_out, and_2_out, and_3_out, and_4_out, and_5_out);
endmodule

module for_arrive (
  input  s2_prime,
  input  s1_prime,
  input  s0_prime,
  input  clk,
  input  reset,
  output out_6
);

  wire [2:0] register_3_q;

  Register #(.width(1)) register_1 (.D(s2_prime), .Q(register_3_q[2]), .clk(clk), .clr(reset));  // open: en
  Register #(.width(1)) register_2 (.D(s1_prime), .Q(register_3_q[1]), .clk(clk), .clr(reset));  // open: en
  Register #(.width(1)) register_3 (.D(s0_prime), .Q(register_3_q[0]), .clk(clk), .clr(reset));  // open: en
  Comparator #(.width(3), .mode("unsigned")) comparator_1 (.a(register_3_q), .b(3'b100), .eq(out_6));  // open: gt, lt
endmodule
