// Logisim project ftoi(附加题).circ as structural Verilog: 1 circuit, main circuit ftoi
module ftoi (
  input  [15:0] float_15_0,
  output [31:0] out_2
);

  wire or_1_out, \输出0__1 , \输出0__2 , \输出0__3 ;
  wire [4:0] \左移数 ;
  wire [10:0] bit_extender_1_out;
  wire [31:0] adder_1_out, bit_extender_2_out, multiplexer_1_out, not_1_out, shifter_1_out, \未判断符号 ;

  // Probe on float_15_0[9:0]
  assign bit_extender_1_out = {{1{1'b1}}, float_15_0[9:0]};  // Bit_Extender bit_extender_1
  // Probe on bit_extender_1_out
  assign bit_extender_2_out = {{21{1'b0}}, bit_extender_1_out};  // Bit_Extender bit_extender_2
  Subtractor #(.width(5)) subtractor_1 (
    .a(float_15_0[14:10]), .b(5'b01111), .out(\左移数 ), .bout(\输出0__1 ));  // open: bin
  assign not_1_out = ~\未判断符号 ;  // NOT_Gate not_1, 32 bits wide
  Adder #(.width(32)) adder_1 (.a(not_1_out), .b(32'h1), .out(adder_1_out));  // open: cin, cout
  // Probe on bit_extender_2_out
  // Probe on shifter_1_out
  Shifter #(.width(32)) shifter_1 (.in(bit_extender_2_out), .\dist (\左移数 ), .out(shifter_1_out));
  Comparator #(.width(5), .mode("unsigned")) comparator_1 (
    .a(float_15_0[14:10]), .b({5{1'b0}}), .eq(\输出0__2 ));  // open: gt, lt
  Multiplexer #(.width(32), .enable("false")) multiplexer_1 (
    .in0(\未判断符号 ), .in1(adder_1_out), .out(multiplexer_1_out), .sel(float_15_0[15]));
  Shifter #(.width(32), .shift("ar")) shifter_2 (.in(shifter_1_out), .\dist (5'b01010), .out(\未判断符号 ));
  or or_1 (or_1_out, \输出0__1 , \输出0__2 , \输出0__3 );
  Comparator #(.width(5), .mode("unsigned")) comparator_2 (
    .a(float_15_0[14:10]), .b({5{1'b1}}), .eq(\输出0__3 ));  // open: gt, lt
  Multiplexer #(.width(32), .enable("false")) multiplexer_2 (
    .in0(multiplexer_1_out), .in1({32{1'b0}}), .out(out_2), .sel(or_1_out));

  // Other names for the same wires on the sheet: 底数[9:0] = float_15_0[9:0]; 指数[4:0] = float_15_0[14:10];
  //   符号位 = float_15_0[15]
endmodule
