// Logisim project 实现GRF(P0.Q2).circ as structural Verilog: 1 circuit, main circuit grf
module grf (
  input  [4:0] A1,
  input  CLK,
  input  [4:0] A2,
  input  [4:0] A3,
  input  RESET,
  input  WE,
  input  [31:0] WD,
  output [31:0] RD1,
  output [31:0] RD2
);

  wire clk_t;
  wire [31:0] IN_0, IN_1, IN_2, IN_3, IN_4, IN_5, IN_6, IN_7, IN_8, IN_9, IN_10, IN_11, IN_12, IN_13, IN_14,
       IN_15, IN_16, IN_17, IN_18, IN_19, IN_20, IN_21, IN_22, IN_23, IN_24, IN_25, IN_26, IN_27, IN_28,
       IN_29, IN_30, IN_31, OUT_0, OUT_1, OUT_2, OUT_3, OUT_4, OUT_5, OUT_6, OUT_7, OUT_8, OUT_9, OUT_10,
       OUT_11, OUT_12, OUT_13, OUT_14, OUT_15, OUT_16, OUT_17, OUT_18, OUT_19, OUT_20, OUT_21, OUT_22,
       OUT_23, OUT_24, OUT_25, OUT_26, OUT_27, OUT_28, OUT_29, OUT_30, OUT_31;

  Demultiplexer #(.select(5), .width(32), .tristate("true")) demultiplexer_1 (
    .out0(IN_0), .out1(IN_1), .out2(IN_2), .out3(IN_3), .out4(IN_4), .out5(IN_5), .out6(IN_6), .out7(IN_7),
    .out8(IN_8), .out9(IN_9), .out10(IN_10), .out11(IN_11), .out12(IN_12), .out13(IN_13), .out14(IN_14),
    .out15(IN_15), .out16(IN_16), .out17(IN_17), .out18(IN_18), .out19(IN_19), .out20(IN_20), .out21(IN_21),
    .out22(IN_22), .out23(IN_23), .out24(IN_24), .out25(IN_25), .out26(IN_26), .out27(IN_27), .out28(IN_28),
    .out29(IN_29), .out30(IN_30), .out31(IN_31), .in(WD), .sel(A3));  // open: en
  Clock clock_1 (.out(clk_t));
  Multiplexer #(.select(5), .width(32)) multiplexer_1 (
    .in0(OUT_0), .in1(OUT_1), .in2(OUT_2), .in3(OUT_3), .in4(OUT_4), .in5(OUT_5), .in6(OUT_6), .in7(OUT_7),
    .in8(OUT_8), .in9(OUT_9), .in10(OUT_10), .in11(OUT_11), .in12(OUT_12), .in13(OUT_13), .in14(OUT_14),
    .in15(OUT_15), .in16(OUT_16), .in17(OUT_17), .in18(OUT_18), .in19(OUT_19), .in20(OUT_20), .in21(OUT_21),
    .in22(OUT_22), .in23(OUT_23), .in24(OUT_24), .in25(OUT_25), .in26(OUT_26), .in27(OUT_27), .in28(OUT_28),
    .in29(OUT_29), .in30(OUT_30), .in31(OUT_31), .out(RD1), .sel(A1));  // open: en
  Multiplexer #(.select(5), .width(32)) multiplexer_2 (
    .in0(OUT_0), .in1(OUT_1), .in2(OUT_2), .in3(OUT_3), .in4(OUT_4), .in5(OUT_5), .in6(OUT_6), .in7(OUT_7),
    .in8(OUT_8), .in9(OUT_9), .in10(OUT_10), .in11(OUT_11), .in12(OUT_12), .in13(OUT_13), .in14(OUT_14),
    .in15(OUT_15), .in16(OUT_16), .in17(OUT_17), .in18(OUT_18), .in19(OUT_19), .in20(OUT_20), .in21(OUT_21),
    .in22(OUT_22), .in23(OUT_23), .in24(OUT_24), .in25(OUT_25), .in26(OUT_26), .in27(OUT_27), .in28(OUT_28),
    .in29(OUT_29), .in30(OUT_30), .in31(OUT_31), .out(RD2), .sel(A2));  // open: en
  Register #(.width(32)) NO_0 (.D(IN_0), .en(WE), .Q(OUT_0), .clk(clk_t), .clr(1'b1));
  Register #(.width(32)) NO_4 (.D(IN_4), .en(WE), .Q(OUT_4), .clk(clk_t), .clr(RESET));
  Register #(.width(32)) NO_8 (.D(IN_8), .en(WE), .Q(OUT_8), .clk(clk_t), .clr(RESET));
  Register #(.width(32)) NO_12 (.D(IN_12), .en(WE), .Q(OUT_12), .clk(clk_t), .clr(RESET));
  Register #(.width(32)) NO_16 (.D(IN_16), .en(WE), .Q(OUT_16), .clk(clk_t), .clr(RESET));
  Register #(.width(32)) NO_20 (.D(IN_20), .en(WE), .Q(OUT_20), .clk(clk_t), .clr(RESET));
  Register #(.width(32)) NO_24 (.D(IN_24), .en(WE), .Q(OUT_24), .clk(clk_t), .clr(RESET));
  Register #(.width(32)) NO_28 (.D(IN_28), .en(WE), .Q(OUT_28), .clk(clk_t), .clr(RESET));
  Register #(.width(32)) NO_1 (.D(IN_1), .en(WE), .Q(OUT_1), .clk(clk_t), .clr(RESET));
  Register #(.width(32)) NO_5 (.D(IN_5), .en(WE), .Q(OUT_5), .clk(clk_t), .clr(RESET));
  Register #(.width(32)) NO_9 (.D(IN_9), .en(WE), .Q(OUT_9), .clk(clk_t), .clr(RESET));
  Register #(.width(32)) NO_13 (.D(IN_13), .en(WE), .Q(OUT_13), .clk(clk_t), .clr(RESET));
  Register #(.width(32)) NO_17 (.D(IN_17), .en(WE), .Q(OUT_17), .clk(clk_t), .clr(RESET));
  Register #(.width(32)) NO_21 (.D(IN_21), .en(WE), .Q(OUT_21), .clk(clk_t), .clr(RESET));
  Register #(.width(32)) NO_25 (.D(IN_25), .en(WE), .Q(OUT_25), .clk(clk_t), .clr(RESET));
  Register #(.width(32)) NO_29 (.D(IN_29), .en(WE), .Q(OUT_29), .clk(clk_t), .clr(RESET));
  Register #(.width(32)) NO_2 (.D(IN_2), .en(WE), .Q(OUT_2), .clk(clk_t), .clr(RESET));
  Register #(.width(32)) NO_6 (.D(IN_6), .en(WE), .Q(OUT_6), .clk(clk_t), .clr(RESET));
  Register #(.width(32)) NO_10 (.D(IN_10), .en(WE), .Q(OUT_10), .clk(clk_t), .clr(RESET));
  Register #(.width(32)) NO_14 (.D(IN_14), .en(WE), .Q(OUT_14), .clk(clk_t), .clr(RESET));
  Register #(.width(32)) NO_18 (.D(IN_18), .en(WE), .Q(OUT_18), .clk(clk_t), .clr(RESET));
  Register #(.width(32)) NO_22 (.D(IN_22), .en(WE), .Q(OUT_22), .clk(clk_t), .clr(RESET));
  Register #(.width(32)) NO_26 (.D(IN_26), .en(WE), .Q(OUT_26), .clk(clk_t), .clr(RESET));
  Register #(.width(32)) NO_30 (.D(IN_30), .en(WE), .Q(OUT_30), .clk(clk_t), .clr(RESET));
  Register #(.width(32)) NO_3 (.D(IN_3), .en(WE), .Q(OUT_3), .clk(clk_t), .clr(RESET));
  Register #(.width(32)) NO_7 (.D(IN_7), .en(WE), .Q(OUT_7), .clk(clk_t), .clr(RESET));
  Register #(.width(32)) NO_11 (.D(IN_11), .en(WE), .Q(OUT_11), .clk(clk_t), .clr(RESET));
  Register #(.width(32)) NO_15 (.D(IN_15), .en(WE), .Q(OUT_15), .clk(clk_t), .clr(RESET));
  Register #(.width(32)) NO_19 (.D(IN_19), .en(WE), .Q(OUT_19), .clk(clk_t), .clr(RESET));
  Register #(.width(32)) NO_23 (.D(IN_23), .en(WE), .Q(OUT_23), .clk(clk_t), .clr(RESET));
  Register #(.width(32)) NO_27 (.D(IN_27), .en(WE), .Q(OUT_27), .clk(clk_t), .clr(RESET));
  Register #(.width(32)) NO_31 (.D(IN_31), .en(WE), .Q(OUT_31), .clk(clk_t), .clr(RESET));

  // Other names for the same wires on the sheet: out_address1[31:0] = RD1; out_address2[31:0] = RD2;
  //   read_address1[4:0] = A1; read_address2[4:0] = A2; write_address[4:0] = A3; write_data[31:0] = WD;
  //   write_enable = WE
endmodule
