// Logisim project 课上第三题.circ as structural Verilog: 1 circuit, main circuit main
module main (
  input  [4:0] in_1,
  output [31:0] out_2
);

  wire clk, comparator_1_eq;
  wire [1:0] adder_1_out, counter_2_q;
  wire [4:0] counter_1_q;
  wire [31:0] adder_2_out, and_1_out, multiplexer_1_out, r, r_1, r_2;

  Clock clock_1 (.out(clk));
  Counter #(.width(5), .max('h1f), .ongoal("stay")) counter_1 (
    .Q(counter_1_q), .clk(clk));  // open: load, D, count, carry, clr
  Comparator #(.width(5)) comparator_1 (.a(in_1), .b(counter_1_q), .eq(comparator_1_eq));  // open: gt, lt
  Register #(.width(32)) register_1 (.D(r), .Q(out_2), .clk(comparator_1_eq));  // open: en, clr
  Counter #(.width(2), .max('h2), .ongoal("stay")) counter_2 (
    .Q(counter_2_q), .clk(clk));  // open: load, D, count, carry, clr
  Adder #(.width(2)) adder_1 (.a(2'b01), .b(counter_2_q), .out(adder_1_out));  // open: cin, cout
  assign and_1_out = r_1 & r_2;  // AND_Gate and_1, 32 bits wide
  Multiplexer #(.select(2), .width(32)) multiplexer_1 (
    .in1(32'h1), .in2(32'h1), .in3(r), .out(multiplexer_1_out), .sel(adder_1_out));  // open: in0, en
  // Probe on adder_1_out
  Adder #(.width(32)) adder_2 (.a(and_1_out), .b(multiplexer_1_out), .out(adder_2_out));  // open: cin, cout
  // Probe on adder_2_out
  Register #(.width(32)) register_2 (.D(r_1), .Q(r_2), .clk(clk));  // open: en, clr
  Register #(.width(32)) register_3 (.D(r), .Q(r_1), .clk(clk));  // open: en, clr
  Register #(.width(32)) register_4 (.D(adder_2_out), .Q(r), .clk(clk));  // open: en, clr
endmodule
