// Logisim project p3_cpu - 2.circ as structural Verilog: 9 circuits, main circuit GRF
module main (
  input  in_1,
  output [31:0] out_2,
  output out_3,
  output [4:0] out_4,
  output [31:0] out_5,
  output out_6,
  output [4:0] out_7,
  output [31:0] out_8
);

  wire ALUSrc, ALUZero, Branch, clk, comparator_1_eq, comparator_2_eq, jump, lui, not_1_out, not_2_out,
       RegDst, REGorMEM, s, ZeroEXT;
  wire [2:0] maindecoder_1_aluop;
  wire [3:0] ALUControl;
  wire [4:0] multiplexer_2_out;
  wire [31:0] dm_1_rd, ext_1_out_3, grf_1_rd1, MemAddr, multiplexer_4_out, multiplexer_5_out,
       multiplexer_6_out, npc_1_npc, register_1_q, shamt_32bit, shifter_1_out, shifter_2_out;

  Clock clock_1 (.out(clk));
  Comparator #(.width(6), .mode("unsigned")) comparator_1 (
    .a(out_2[31:26]), .b({6{1'b0}}), .eq(comparator_1_eq));  // open: gt, lt
  Comparator #(.width(5), .mode("unsigned")) comparator_2 (
    .a(out_2[10:6]), .b({5{1'b0}}), .eq(comparator_2_eq));  // open: gt, lt
  not not_1 (not_1_out, comparator_2_eq);
  NPC npc_1 (.PC(register_1_q), ._26imm(out_2[25:0]), .NPC(npc_1_npc), .ALUZero(ALUZero), .Branch(Branch), .jump(jump));
  Register #(.width(32)) register_1 (.D(npc_1_npc), .Q(register_1_q), .clk(clk), .clr(in_1));  // open: en
  and and_1 (s, comparator_1_eq, not_1_out);
  IM im_1 (.in_1(register_1_q), .out_2(out_2));
  assign shamt_32bit = {{27{1'b0}}, out_2[10:6]};  // Bit_Extender bit_extender_1
  ALUDecoder aludecoder_1 (.Funct(out_2[5:0]), .ALUControl(ALUControl), .ALUOp(maindecoder_1_aluop));
  Multiplexer #(.width(5), .enable("false")) multiplexer_1 (
    .in0(out_2[15:11]), .in1(out_2[20:16]), .out(out_4), .sel(RegDst));
  EXT ext_1 (.IMM(out_2[15:0]), .out_3(ext_1_out_3), .ZeroExt(ZeroEXT));
  MainDecoder maindecoder_1 (
    .Opcode_5_0(out_2[31:26]), .REGorMEM(REGorMEM), .MemWrite(out_6), .Branch(Branch), .ALUSrc(ALUSrc),
    .RegDst(RegDst), .RegWrite(out_3), .ZeroEXT(ZeroEXT), .Lui(lui), .ALUOp(maindecoder_1_aluop), .jump(jump));
  Multiplexer #(.width(5), .enable("false")) multiplexer_2 (
    .in0(out_2[25:21]), .in1(out_2[20:16]), .out(multiplexer_2_out), .sel(s));
  Multiplexer #(.width(32), .enable("false")) multiplexer_3 (
    .in0(shifter_1_out), .in1(multiplexer_6_out), .out(out_5), .sel(not_2_out));
  Shifter #(.width(32)) shifter_1 (.in(ext_1_out_3), .\dist (5'b10000), .out(shifter_1_out));
  Clock clock_2 ();  // open: out
  not not_2 (not_2_out, lui);
  GRF grf_1 (
    .A1(multiplexer_2_out), .A2(out_2[20:16]), .A3(out_4), .WD(out_5), .RD1(grf_1_rd1), .RD2(out_8),
    .CLK(clk), .RESET(in_1), .WE(out_3));
  Multiplexer #(.width(32), .enable("false")) multiplexer_4 (
    .in0(out_8), .in1(ext_1_out_3), .out(multiplexer_4_out), .sel(ALUSrc));
  Bit_Extender #(.in_width(32), .out_width(5)) bit_extender_2 (.in(shifter_2_out), .out(out_7));
  Shifter #(.width(32), .shift("lr")) shifter_2 (.in(MemAddr), .\dist (5'b00010), .out(shifter_2_out));
  Multiplexer #(.width(32), .enable("false")) multiplexer_5 (
    .in0(multiplexer_4_out), .in1(shamt_32bit), .out(multiplexer_5_out), .sel(s));
  ALU alu_1 (.A(grf_1_rd1), .B(multiplexer_5_out), .zero(ALUZero), .ALUResult(MemAddr), .FUNC(ALUControl));
  DM dm_1 (.A(MemAddr), .WD(out_8), .RD(dm_1_rd), .clk(clk), .in_2(out_6), .in_5(in_1));
  Multiplexer #(.width(32), .enable("false")) multiplexer_6 (
    .in0(MemAddr), .in1(dm_1_rd), .out(multiplexer_6_out), .sel(REGorMEM));

  // Other names for the same wires on the sheet: _26imm[25:0] = out_2[25:0]; funct[5:0] = out_2[5:0];
  //   imm_offset[15:0] = out_2[15:0]; instr[31:0] = out_2; shamt[4:0] = out_2[10:6]; rd[4:0] = out_2[15:11];
  //   rt[4:0] = out_2[20:16]; rs[4:0] = out_2[25:21]; op[5:0] = out_2[31:26]; MemWrite = out_6; RegAddr[4:0] = out_4;
  //   RegData[31:0] = out_5; RegWrite = out_3; rst = in_1; WriteData[31:0] = out_8

  // Notes on the sheet:
  //   一战
  //   判断是否为R指令中的移位指令
  //   instructions: addu, subu, and, or, ori, lw, sw, beq, 
  //   lui, slt, sll, srl, sra, j, nop
  //   pc
  //   npc
  //   instr
  //   0:from reg, 1:from mem
endmodule

module NPC (
  input  [31:0] PC,
  input  [25:0] _26imm,
  input  ALUZero,
  input  Branch,
  input  jump,
  output [31:0] NPC
);

  wire and_1_out;
  wire [15:0] bit_extender_1_out;
  wire [31:0] adder_1_out, adder_2_out, bit_extender_2_out, multiplexer_1_out, shifter_1_out;

  Bit_Extender #(.in_width(26)) bit_extender_1 (.in(_26imm), .out(bit_extender_1_out));
  assign bit_extender_2_out = {{16{bit_extender_1_out[15]}}, bit_extender_1_out};  // Bit_Extender bit_extender_2
  Adder #(.width(32)) adder_1 (.a(PC), .b(32'h4), .out(adder_1_out));  // open: cin, cout
  Shifter #(.width(32)) shifter_1 (.in(bit_extender_2_out), .\dist (5'b00010), .out(shifter_1_out));
  Adder #(.width(32)) adder_2 (.a(adder_1_out), .b(shifter_1_out), .out(adder_2_out));  // open: cin, cout
  Multiplexer #(.width(32), .enable("false")) multiplexer_1 (
    .in0(adder_1_out), .in1(adder_2_out), .out(multiplexer_1_out), .sel(and_1_out));
  and and_1 (and_1_out, ALUZero, Branch);
  Multiplexer #(.width(32), .enable("false")) multiplexer_2 (
    .in0(multiplexer_1_out), .in1({PC[31:28], _26imm, 2'b00}), .out(NPC), .sel(jump));

  // Other names for the same wires on the sheet: PC_31_28[3:0] = PC[31:28]; J = jump
endmodule

module IM (
  input  [31:0] in_1,
  output [31:0] out_2
);

  wire [4:0] bit_extender_1_out;
  wire [31:0] shifter_1_out;

  Shifter #(.width(32), .shift("lr")) shifter_1 (.in(in_1), .\dist (5'b00010), .out(shifter_1_out));
  Bit_Extender #(.in_width(32), .out_width(5)) bit_extender_1 (.in(shifter_1_out), .out(bit_extender_1_out));
  ROM #(.addrWidth(5), .dataWidth(32)) rom_1 (.addr(bit_extender_1_out), .data(out_2));  // open: sel

  // Notes on the sheet:
  //   contents of rom_1 (hex, n*v repeats v):
  //   341c0000 341d0000 340080f8 36ee0367 3593769c 34dda539 3465c5dc 34be0ff1 3472af1d 35566602 35fe72a7
  //   3437ff23 37b9649e 3690bf9b 37fe4e0c 3711f49d 3c113bfe 3c057433 3c03c451 3c04c431 3c1c24d9 3c1bf0da
  //   3c0ccc68 3c0a118d 3c1021ea 3c0004d3 3c16115b 3c184f06 3c1215de 1000ffff
endmodule

module GRF (
  input  [4:0] A1,
  input  [4:0] A2,
  input  [4:0] A3,
  input  CLK,
  input  RESET,
  input  WE,
  input  [31:0] WD,
  output [31:0] RD1,
  output [31:0] RD2
);

  wire [31:0] IN_0, IN_1, IN_2, IN_3, IN_4, IN_5, IN_6, IN_7, IN_8, IN_9, IN_10, IN_11, IN_12, IN_13, IN_14,
       IN_15, IN_16, IN_17, IN_18, IN_19, IN_20, IN_21, IN_22, IN_23, IN_24, IN_25, IN_26, IN_27, IN_28,
       IN_29, IN_30, IN_31, OUT_0, OUT_1, OUT_2, OUT_3, OUT_4, OUT_5, OUT_6, OUT_7, OUT_8, OUT_9, OUT_10,
       OUT_11, OUT_12, OUT_13, OUT_14, OUT_15, OUT_16, OUT_17, OUT_18, OUT_19, OUT_20, OUT_21, OUT_22,
       OUT_23, OUT_24, OUT_25, OUT_26, OUT_27, OUT_28, OUT_29, OUT_30, OUT_31;

  // Probe on A3
  Demultiplexer #(.select(5), .width(32), .tristate("true")) demultiplexer_1 (
    .out0(IN_0), .out1(IN_1), .out2(IN_2), .out3(IN_3), .out4(IN_4), .out5(IN_5), .out6(IN_6), .out7(IN_7),
    .out8(IN_8), .out9(IN_9), .out10(IN_10), .out11(IN_11), .out12(IN_12), .out13(IN_13), .out14(IN_14),
    .out15(IN_15), .out16(IN_16), .out17(IN_17), .out18(IN_18), .out19(IN_19), .out20(IN_20), .out21(IN_21),
    .out22(IN_22), .out23(IN_23), .out24(IN_24), .out25(IN_25), .out26(IN_26), .out27(IN_27), .out28(IN_28),
    .out29(IN_29), .out30(IN_30), .out31(IN_31), .in(WD), .sel(A3));  // open: en
  // Probe on WD
  Multiplexer #(.select(5), .width(32)) multiplexer_1 (
    .in0(OUT_0), .in1(OUT_1), .in2(OUT_2), .in3(OUT_3), .in4(OUT_4), .in5(OUT_5), .in6(OUT_6), .in7(OUT_7),
    .in8(OUT_8), .in9(OUT_9), .in10(OUT_10), .in11(OUT_11), .in12(OUT_12), .in13(OUT_13), .in14(OUT_14),
    .in15(OUT_15), .in16(OUT_16), .in17(OUT_17), .in18(OUT_18), .in19(OUT_19), .in20(OUT_20), .in21(OUT_21),
    .in22(OUT_22), .in23(OUT_23), .in24(OUT_24), .in25(OUT_25), .in26(OUT_26), .in27(OUT_27), .in28(OUT_28),
    .in29(OUT_29), .in30(OUT_30), .in31(OUT_31), .out(RD1), .sel(A1));  // open: en
  Multiplexer #(.select(5), .width(32)) multiplexer_2 (
    .in0(OUT_0), .in1(OUT_1), .in2(OUT_2), .in3(OUT_3), .in4(OUT_4), .in5(OUT_5), .in6(OUT_6), .in7(OUT_7),
    .in8(OUT_8), .in9(OUT_9), .in10(OUT_10), .in11(OUT_11), .in12(OUT_12), .in13(OUT_13), .in14(OUT_14),
    .in15(OUT_15), .in16(OUT_16), .in17(OUT_17), .in18(OUT_18), .in19(OUT_19), .in20(OUT_20), .in21(OUT_21),
    .in22(OUT_22), .in23(OUT_23), .in24(OUT_24), .in25(OUT_25), .in26(OUT_26), .in27(OUT_27), .in28(OUT_28),
    .in29(OUT_29), .in30(OUT_30), .in31(OUT_31), .out(RD2), .sel(A2));  // open: en
  Register #(.width(32)) NO_0 (.D(IN_0), .en(WE), .Q(OUT_0), .clk(CLK), .clr(1'b1));
  Register #(.width(32)) NO_4 (.D(IN_4), .en(WE), .Q(OUT_4), .clk(CLK), .clr(RESET));
  Register #(.width(32)) NO_8 (.D(IN_8), .en(WE), .Q(OUT_8), .clk(CLK), .clr(RESET));
  Register #(.width(32)) NO_12 (.D(IN_12), .en(WE), .Q(OUT_12), .clk(CLK), .clr(RESET));
  Register #(.width(32)) NO_16 (.D(IN_16), .en(WE), .Q(OUT_16), .clk(CLK), .clr(RESET));
  Register #(.width(32)) NO_20 (.D(IN_20), .en(WE), .Q(OUT_20), .clk(CLK), .clr(RESET));
  Register #(.width(32)) NO_24 (.D(IN_24), .en(WE), .Q(OUT_24), .clk(CLK), .clr(RESET));
  Register #(.width(32)) NO_28 (.D(IN_28), .en(WE), .Q(OUT_28), .clk(CLK), .clr(RESET));
  Register #(.width(32)) NO_1 (.D(IN_1), .en(WE), .Q(OUT_1), .clk(CLK), .clr(RESET));
  Register #(.width(32)) NO_5 (.D(IN_5), .en(WE), .Q(OUT_5), .clk(CLK), .clr(RESET));
  Register #(.width(32)) NO_9 (.D(IN_9), .en(WE), .Q(OUT_9), .clk(CLK), .clr(RESET));
  Register #(.width(32)) NO_13 (.D(IN_13), .en(WE), .Q(OUT_13), .clk(CLK), .clr(RESET));
  Register #(.width(32)) NO_17 (.D(IN_17), .en(WE), .Q(OUT_17), .clk(CLK), .clr(RESET));
  Register #(.width(32)) NO_21 (.D(IN_21), .en(WE), .Q(OUT_21), .clk(CLK), .clr(RESET));
  Register #(.width(32)) NO_25 (.D(IN_25), .en(WE), .Q(OUT_25), .clk(CLK), .clr(RESET));
  Register #(.width(32)) NO_29 (.D(IN_29), .en(WE), .Q(OUT_29), .clk(CLK), .clr(RESET));
  Register #(.width(32)) NO_2 (.D(IN_2), .en(WE), .Q(OUT_2), .clk(CLK), .clr(RESET));
  Register #(.width(32)) NO_6 (.D(IN_6), .en(WE), .Q(OUT_6), .clk(CLK), .clr(RESET));
  Register #(.width(32)) NO_10 (.D(IN_10), .en(WE), .Q(OUT_10), .clk(CLK), .clr(RESET));
  Register #(.width(32)) NO_14 (.D(IN_14), .en(WE), .Q(OUT_14), .clk(CLK), .clr(RESET));
  Register #(.width(32)) NO_18 (.D(IN_18), .en(WE), .Q(OUT_18), .clk(CLK), .clr(RESET));
  Register #(.width(32)) NO_22 (.D(IN_22), .en(WE), .Q(OUT_22), .clk(CLK), .clr(RESET));
  Register #(.width(32)) NO_26 (.D(IN_26), .en(WE), .Q(OUT_26), .clk(CLK), .clr(RESET));
  Register #(.width(32)) NO_30 (.D(IN_30), .en(WE), .Q(OUT_30), .clk(CLK), .clr(RESET));
  Register #(.width(32)) NO_3 (.D(IN_3), .en(WE), .Q(OUT_3), .clk(CLK), .clr(RESET));
  Register #(.width(32)) NO_7 (.D(IN_7), .en(WE), .Q(OUT_7), .clk(CLK), .clr(RESET));
  Register #(.width(32)) NO_11 (.D(IN_11), .en(WE), .Q(OUT_11), .clk(CLK), .clr(RESET));
  Register #(.width(32)) NO_15 (.D(IN_15), .en(WE), .Q(OUT_15), .clk(CLK), .clr(RESET));
  Register #(.width(32)) NO_19 (.D(IN_19), .en(WE), .Q(OUT_19), .clk(CLK), .clr(RESET));
  Register #(.width(32)) NO_23 (.D(IN_23), .en(WE), .Q(OUT_23), .clk(CLK), .clr(RESET));
  Register #(.width(32)) NO_27 (.D(IN_27), .en(WE), .Q(OUT_27), .clk(CLK), .clr(RESET));
  Register #(.width(32)) NO_31 (.D(IN_31), .en(WE), .Q(OUT_31), .clk(CLK), .clr(RESET));

  // Other names for the same wires on the sheet: out_address1[31:0] = RD1; out_address2[31:0] = RD2;
  //   read_address1[4:0] = A1; read_address2[4:0] = A2; write_address[4:0] = A3; write_data[31:0] = WD;
  //   write_enable = WE
endmodule

module ALU (
  input  [3:0] FUNC,
  input  [31:0] A,
  input  [31:0] B,
  output zero,
  output [31:0] ALUResult
);

  wire comparator_1_eq, comparator_2_eq, comparator_3_eq;
  wire [4:0] bit_extender_1_out, bit_extender_2_out, bit_extender_3_out;
  wire [31:0] adder_1_out, AND_out, bit_extender_4_out, multiplexer_1_out, multiplexer_5_out, not_1_out,
       or_2_out, OR_out, shifter_1_out, shifter_2_out, shifter_3_out, SLL, SRA, SRL;

  // Probe on A
  // Probe on B
  Bit_Extender #(.in_width(32), .out_width(5)) bit_extender_1 (.in(B), .out(bit_extender_1_out));
  Bit_Extender #(.in_width(32), .out_width(5)) bit_extender_2 (.in(B), .out(bit_extender_2_out));
  Bit_Extender #(.in_width(32), .out_width(5)) bit_extender_3 (.in(B), .out(bit_extender_3_out));
  Shifter #(.width(32)) shifter_1 (.in(A), .\dist (bit_extender_1_out), .out(shifter_1_out));
  // Probe on 3'b000
  Shifter #(.width(32), .shift("lr")) shifter_2 (.in(A), .\dist (bit_extender_2_out), .out(shifter_2_out));
  // Probe on 3'b001
  Shifter #(.width(32), .shift("ar")) shifter_3 (.in(A), .\dist (bit_extender_3_out), .out(shifter_3_out));
  // Probe on 3'b010
  Multiplexer #(.width(32), .enable("false")) multiplexer_1 (
    .in0(B), .in1(not_1_out), .out(multiplexer_1_out), .sel(FUNC[2]));
  assign not_1_out = ~B;  // NOT_Gate not_1, 32 bits wide
  Multiplexer #(.width(32), .enable("false")) multiplexer_2 (
    .in0({32{1'b0}}), .in1(shifter_1_out), .out(SLL), .sel(comparator_1_eq));
  Comparator #(.width(3), .mode("unsigned")) comparator_1 (
    .a(3'b000), .b(FUNC[2:0]), .eq(comparator_1_eq));  // open: gt, lt
  Multiplexer #(.width(32), .enable("false")) multiplexer_3 (
    .in0({32{1'b0}}), .in1(shifter_2_out), .out(SRL), .sel(comparator_2_eq));
  Comparator #(.width(3), .mode("unsigned")) comparator_2 (
    .a(3'b001), .b(FUNC[2:0]), .eq(comparator_2_eq));  // open: gt, lt
  Multiplexer #(.width(32), .enable("false")) multiplexer_4 (
    .in0({32{1'b0}}), .in1(shifter_3_out), .out(SRA), .sel(comparator_3_eq));
  Comparator #(.width(3), .mode("unsigned")) comparator_3 (
    .a(3'b010), .b(FUNC[2:0]), .eq(comparator_3_eq));  // open: gt, lt
  assign AND_out = A & multiplexer_1_out;  // AND_Gate AND, 32 bits wide
  assign OR_out = A | multiplexer_1_out;  // OR_Gate OR, 32 bits wide
  Adder #(.width(32)) adder_1 (.a(A), .b(multiplexer_1_out), .out(adder_1_out), .cin(FUNC[2]));  // open: cout
  assign bit_extender_4_out = {{31{1'b0}}, adder_1_out[31]};  // Bit_Extender bit_extender_4
  Multiplexer #(.select(2), .width(32), .enable("false")) multiplexer_5 (
    .in0(AND_out), .in1(OR_out), .in2(adder_1_out), .in3(bit_extender_4_out), .out(multiplexer_5_out),
    .sel(FUNC[1:0]));
  // Probe on multiplexer_5_out
  Comparator #(.width(32)) comparator_4 (.a(multiplexer_5_out), .b({32{1'b0}}), .eq(zero));  // open: gt, lt
  assign or_2_out = SLL | SRL | SRA;  // OR_Gate or_2, 32 bits wide
  // Probe on ALUResult
  Multiplexer #(.width(32), .enable("false")) multiplexer_6 (
    .in0(multiplexer_5_out), .in1(or_2_out), .out(ALUResult), .sel(FUNC[3]));

  // Other names for the same wires on the sheet: F_0_1[1:0] = FUNC[1:0]; F_2_0[2:0] = FUNC[2:0]; F_2 = FUNC[2];
  //   F_3 = FUNC[3]

  // Notes on the sheet:
  //   SLL
  //   SRL
  //   SRA
  //   取符号位并0扩展
endmodule

module DM (
  input  clk,
  input  in_2,
  input  [31:0] A,
  input  [31:0] WD,
  input  in_5,
  output [31:0] RD
);

  wire [4:0] bit_extender_1_out;
  wire [31:0] shifter_1_out;

  // Probe on shifter_1_out
  Bit_Extender #(.in_width(32), .out_width(5)) bit_extender_1 (.in(shifter_1_out), .out(bit_extender_1_out));
  Shifter #(.width(32), .shift("lr")) shifter_1 (.in(A), .\dist (5'b00010), .out(shifter_1_out));
  // Probe on WD
  // Probe on bit_extender_1_out
  RAM #(.addrWidth(5), .dataWidth(32), .bus("separate")) ram_1 (
    .addr(bit_extender_1_out), .din(WD), .data(RD), .str(in_2), .clk(clk), .clr(in_5));  // open: sel, ld

  // Other names for the same wires on the sheet: rst = in_5; WE = in_2
endmodule

module EXT (
  input  ZeroExt,
  input  [15:0] IMM,
  output [31:0] out_3
);

  wire [31:0] bit_extender_1_out, bit_extender_2_out;

  assign bit_extender_1_out = {{16{IMM[15]}}, IMM};  // Bit_Extender bit_extender_1
  Multiplexer #(.width(32), .enable("false")) multiplexer_1 (
    .in0(bit_extender_1_out), .in1(bit_extender_2_out), .out(out_3), .sel(ZeroExt));
  assign bit_extender_2_out = {{16{1'b0}}, IMM};  // Bit_Extender bit_extender_2

  // Other names for the same wires on the sheet: zero_ext = ZeroExt
endmodule

module MainDecoder (
  input  [5:0] Opcode_5_0,
  output REGorMEM,
  output MemWrite,
  output Branch,
  output ALUSrc,
  output RegDst,
  output RegWrite,
  output ZeroEXT,
  output Lui,
  output [2:0] ALUOp,
  output jump
);

  wire ALUSrc1, ALUSrc2, ALUSrc3, ALUSrc4, ALUSrc5, ALUSrc6, ALUSrc7, Branch1, Branch2, Branch3, Branch4,
       Branch5, Branch6, Branch7, comparator_1_eq, comparator_2_eq, comparator_3_eq, comparator_4_eq,
       comparator_5_eq, comparator_6_eq, comparator_7_eq, j1, j2, j3, j4, j5, j6, j7, Lui1, Lui2, Lui3, Lui4,
       Lui5, Lui6, Lui7, MemWrite1, MemWrite2, MemWrite3, MemWrite4, MemWrite5, MemWrite6, MemWrite7,
       RegDst1, RegDst2, RegDst3, RegDst4, RegDst5, RegDst6, RegDst7, REGorMEM1, REGorMEM2, REGorMEM3,
       REGorMEM4, REGorMEM5, REGorMEM6, REGorMEM7, RegWrite1, RegWrite2, RegWrite3, RegWrite4, RegWrite5,
       RegWrite6, RegWrite7, ZeroEXT1, ZeroEXT2, ZeroEXT3, ZeroEXT4, ZeroEXT5, ZeroEXT6, ZeroEXT7;
  wire [2:0] ALUOp1, ALUOp2, ALUOp3, ALUOp4, ALUOp5, ALUOp6, ALUOp7;

  // Probe on {6{1'b0}}
  // Probe on 6'b000100
  // Probe on 6'b000010
  Comparator #(.width(6), .mode("unsigned")) comparator_1 (
    .a(Opcode_5_0), .b({6{1'b0}}), .eq(comparator_1_eq));  // open: gt, lt
  Comparator #(.width(6), .mode("unsigned")) comparator_2 (
    .a(Opcode_5_0), .b(6'b000100), .eq(comparator_2_eq));  // open: gt, lt
  Comparator #(.width(6), .mode("unsigned")) comparator_3 (
    .a(Opcode_5_0), .b(6'b000010), .eq(comparator_3_eq));  // open: gt, lt
  Multiplexer #(.enable("false")) multiplexer_1 (.in0(1'b0), .in1(1'b0), .out(REGorMEM1), .sel(comparator_1_eq));
  Multiplexer #(.enable("false")) multiplexer_2 (.in0(1'b0), .in1(1'b0), .out(MemWrite1), .sel(comparator_1_eq));
  Multiplexer #(.enable("false")) multiplexer_3 (.in0(1'b0), .in1(1'b0), .out(Branch1), .sel(comparator_1_eq));
  Multiplexer #(.enable("false")) multiplexer_4 (.in0(1'b0), .in1(1'b0), .out(ALUSrc1), .sel(comparator_1_eq));
  Multiplexer #(.enable("false")) multiplexer_5 (.in0(1'b0), .in1(1'b0), .out(RegDst1), .sel(comparator_1_eq));
  Multiplexer #(.enable("false")) multiplexer_6 (.in0(1'b0), .in1(1'b1), .out(RegWrite1), .sel(comparator_1_eq));
  Multiplexer #(.enable("false")) multiplexer_7 (.in0(1'b0), .in1(1'b0), .out(ZeroEXT1), .sel(comparator_1_eq));
  Multiplexer #(.enable("false")) multiplexer_8 (.in0(1'b0), .in1(1'b0), .out(Lui1), .sel(comparator_1_eq));
  Multiplexer #(.width(3), .enable("false")) multiplexer_9 (
    .in0(3'b000), .in1(3'b010), .out(ALUOp1), .sel(comparator_1_eq));
  // Probe on ALUOp1
  // Probe on 3'b010
  Multiplexer #(.enable("false")) multiplexer_10 (.in0(1'b0), .in1(1'b0), .out(j1), .sel(comparator_1_eq));
  Multiplexer #(.enable("false")) multiplexer_11 (.in0(1'b0), .in1(1'b0), .out(REGorMEM4), .sel(comparator_2_eq));
  Multiplexer #(.enable("false")) multiplexer_12 (.in0(1'b0), .in1(1'b0), .out(MemWrite4), .sel(comparator_2_eq));
  Multiplexer #(.enable("false")) multiplexer_13 (.in0(1'b0), .in1(1'b1), .out(Branch4), .sel(comparator_2_eq));
  Multiplexer #(.enable("false")) multiplexer_14 (.in0(1'b0), .in1(1'b0), .out(ALUSrc4), .sel(comparator_2_eq));
  Multiplexer #(.enable("false")) multiplexer_15 (.in0(1'b0), .in1(1'b0), .out(RegDst4), .sel(comparator_2_eq));
  Multiplexer #(.enable("false")) multiplexer_16 (.in0(1'b0), .in1(1'b0), .out(RegWrite4), .sel(comparator_2_eq));
  Multiplexer #(.enable("false")) multiplexer_17 (.in0(1'b0), .in1(1'b0), .out(ZeroEXT4), .sel(comparator_2_eq));
  Multiplexer #(.enable("false")) multiplexer_18 (.in0(1'b0), .in1(1'b0), .out(Lui4), .sel(comparator_2_eq));
  Multiplexer #(.width(3), .enable("false")) multiplexer_19 (
    .in0(3'b000), .in1(3'b001), .out(ALUOp4), .sel(comparator_2_eq));
  // Probe on ALUOp4
  // Probe on 3'b001
  Multiplexer #(.enable("false")) multiplexer_20 (.in0(1'b0), .in1(1'b0), .out(j4), .sel(comparator_2_eq));
  Multiplexer #(.enable("false")) multiplexer_21 (.in0(1'b0), .in1(1'b0), .out(REGorMEM7), .sel(comparator_3_eq));
  Multiplexer #(.enable("false")) multiplexer_22 (.in0(1'b0), .in1(1'b0), .out(MemWrite7), .sel(comparator_3_eq));
  Multiplexer #(.enable("false")) multiplexer_23 (.in0(1'b0), .in1(1'b0), .out(Branch7), .sel(comparator_3_eq));
  Multiplexer #(.enable("false")) multiplexer_24 (.in0(1'b0), .in1(1'b0), .out(ALUSrc7), .sel(comparator_3_eq));
  Multiplexer #(.enable("false")) multiplexer_25 (.in0(1'b0), .in1(1'b0), .out(RegDst7), .sel(comparator_3_eq));
  Multiplexer #(.enable("false")) multiplexer_26 (.in0(1'b0), .in1(1'b0), .out(RegWrite7), .sel(comparator_3_eq));
  Multiplexer #(.enable("false")) multiplexer_27 (.in0(1'b0), .in1(1'b0), .out(ZeroEXT7), .sel(comparator_3_eq));
  Multiplexer #(.enable("false")) multiplexer_28 (.in0(1'b0), .in1(1'b0), .out(Lui7), .sel(comparator_3_eq));
  Multiplexer #(.width(3), .enable("false")) multiplexer_29 (
    .in0(3'b000), .in1(3'b000), .out(ALUOp7), .sel(comparator_3_eq));
  // Probe on ALUOp7
  // Probe on 3'b000
  Multiplexer #(.enable("false")) multiplexer_30 (.in0(1'b0), .in1(1'b1), .out(j7), .sel(comparator_3_eq));
  // Probe on 6'b100011
  // Probe on 6'b001101
  Comparator #(.width(6), .mode("unsigned")) comparator_4 (
    .a(Opcode_5_0), .b(6'b100011), .eq(comparator_4_eq));  // open: gt, lt
  // Probe on 3'b000
  Comparator #(.width(6), .mode("unsigned")) comparator_5 (
    .a(Opcode_5_0), .b(6'b001101), .eq(comparator_5_eq));  // open: gt, lt
  // Probe on 3'b100
  Multiplexer #(.enable("false")) multiplexer_31 (.in0(1'b0), .in1(1'b1), .out(REGorMEM2), .sel(comparator_4_eq));
  Multiplexer #(.enable("false")) multiplexer_32 (.in0(1'b0), .in1(1'b0), .out(MemWrite2), .sel(comparator_4_eq));
  Multiplexer #(.enable("false")) multiplexer_33 (.in0(1'b0), .in1(1'b0), .out(Branch2), .sel(comparator_4_eq));
  Multiplexer #(.enable("false")) multiplexer_34 (.in0(1'b0), .in1(1'b1), .out(ALUSrc2), .sel(comparator_4_eq));
  Multiplexer #(.enable("false")) multiplexer_35 (.in0(1'b0), .in1(1'b1), .out(RegDst2), .sel(comparator_4_eq));
  Multiplexer #(.enable("false")) multiplexer_36 (.in0(1'b0), .in1(1'b1), .out(RegWrite2), .sel(comparator_4_eq));
  Multiplexer #(.enable("false")) multiplexer_37 (.in0(1'b0), .in1(1'b0), .out(ZeroEXT2), .sel(comparator_4_eq));
  Multiplexer #(.enable("false")) multiplexer_38 (.in0(1'b0), .in1(1'b0), .out(Lui2), .sel(comparator_4_eq));
  Multiplexer #(.width(3), .enable("false")) multiplexer_39 (
    .in0(3'b000), .in1(3'b000), .out(ALUOp2), .sel(comparator_4_eq));
  // Probe on ALUOp2
  Multiplexer #(.enable("false")) multiplexer_40 (.in0(1'b0), .in1(1'b0), .out(j2), .sel(comparator_4_eq));
  Multiplexer #(.enable("false")) multiplexer_41 (.in0(1'b0), .in1(1'b0), .out(REGorMEM5), .sel(comparator_5_eq));
  Multiplexer #(.enable("false")) multiplexer_42 (.in0(1'b0), .in1(1'b0), .out(MemWrite5), .sel(comparator_5_eq));
  Multiplexer #(.enable("false")) multiplexer_43 (.in0(1'b0), .in1(1'b0), .out(Branch5), .sel(comparator_5_eq));
  Multiplexer #(.enable("false")) multiplexer_44 (.in0(1'b0), .in1(1'b1), .out(ALUSrc5), .sel(comparator_5_eq));
  Multiplexer #(.enable("false")) multiplexer_45 (.in0(1'b0), .in1(1'b1), .out(RegDst5), .sel(comparator_5_eq));
  Multiplexer #(.enable("false")) multiplexer_46 (.in0(1'b0), .in1(1'b1), .out(RegWrite5), .sel(comparator_5_eq));
  Multiplexer #(.enable("false")) multiplexer_47 (.in0(1'b0), .in1(1'b1), .out(ZeroEXT5), .sel(comparator_5_eq));
  Multiplexer #(.enable("false")) multiplexer_48 (.in0(1'b0), .in1(1'b0), .out(Lui5), .sel(comparator_5_eq));
  Multiplexer #(.width(3), .enable("false")) multiplexer_49 (
    .in0(3'b000), .in1(3'b100), .out(ALUOp5), .sel(comparator_5_eq));
  // Probe on ALUOp5
  Multiplexer #(.enable("false")) multiplexer_50 (.in0(1'b0), .in1(1'b0), .out(j5), .sel(comparator_5_eq));
  // Probe on 6'b101011
  // Probe on 6'b001111
  Comparator #(.width(6), .mode("unsigned")) comparator_6 (
    .a(Opcode_5_0), .b(6'b101011), .eq(comparator_6_eq));  // open: gt, lt
  Comparator #(.width(6), .mode("unsigned")) comparator_7 (
    .a(Opcode_5_0), .b(6'b001111), .eq(comparator_7_eq));  // open: gt, lt
  Multiplexer #(.enable("false")) multiplexer_51 (.in0(1'b0), .in1(1'b0), .out(REGorMEM3), .sel(comparator_6_eq));
  Multiplexer #(.enable("false")) multiplexer_52 (.in0(1'b0), .in1(1'b1), .out(MemWrite3), .sel(comparator_6_eq));
  Multiplexer #(.enable("false")) multiplexer_53 (.in0(1'b0), .in1(1'b0), .out(Branch3), .sel(comparator_6_eq));
  Multiplexer #(.enable("false")) multiplexer_54 (.in0(1'b0), .in1(1'b1), .out(ALUSrc3), .sel(comparator_6_eq));
  Multiplexer #(.enable("false")) multiplexer_55 (.in0(1'b0), .in1(1'b0), .out(RegDst3), .sel(comparator_6_eq));
  Multiplexer #(.enable("false")) multiplexer_56 (.in0(1'b0), .in1(1'b0), .out(RegWrite3), .sel(comparator_6_eq));
  Multiplexer #(.enable("false")) multiplexer_57 (.in0(1'b0), .in1(1'b0), .out(ZeroEXT3), .sel(comparator_6_eq));
  Multiplexer #(.enable("false")) multiplexer_58 (.in0(1'b0), .in1(1'b0), .out(Lui3), .sel(comparator_6_eq));
  Multiplexer #(.width(3), .enable("false")) multiplexer_59 (
    .in0(3'b000), .in1(3'b000), .out(ALUOp3), .sel(comparator_6_eq));
  // Probe on 3'b000
  Multiplexer #(.enable("false")) multiplexer_60 (.in0(1'b0), .in1(1'b0), .out(j3), .sel(comparator_6_eq));
  Multiplexer #(.enable("false")) multiplexer_61 (.in0(1'b0), .in1(1'b0), .out(REGorMEM6), .sel(comparator_7_eq));
  Multiplexer #(.enable("false")) multiplexer_62 (.in0(1'b0), .in1(1'b0), .out(MemWrite6), .sel(comparator_7_eq));
  Multiplexer #(.enable("false")) multiplexer_63 (.in0(1'b0), .in1(1'b0), .out(Branch6), .sel(comparator_7_eq));
  Multiplexer #(.enable("false")) multiplexer_64 (.in0(1'b0), .in1(1'b0), .out(ALUSrc6), .sel(comparator_7_eq));
  Multiplexer #(.enable("false")) multiplexer_65 (.in0(1'b0), .in1(1'b1), .out(RegDst6), .sel(comparator_7_eq));
  Multiplexer #(.enable("false")) multiplexer_66 (.in0(1'b0), .in1(1'b1), .out(RegWrite6), .sel(comparator_7_eq));
  Multiplexer #(.enable("false")) multiplexer_67 (.in0(1'b0), .in1(1'b0), .out(ZeroEXT6), .sel(comparator_7_eq));
  Multiplexer #(.enable("false")) multiplexer_68 (.in0(1'b0), .in1(1'b1), .out(Lui6), .sel(comparator_7_eq));
  Multiplexer #(.width(3), .enable("false")) multiplexer_69 (
    .in0(3'b000), .in1(3'b000), .out(ALUOp6), .sel(comparator_7_eq));
  // Probe on ALUOp6
  // Probe on 3'b000
  Multiplexer #(.enable("false")) multiplexer_70 (.in0(1'b0), .in1(1'b0), .out(j6), .sel(comparator_7_eq));
  // Probe on ALUOp3
  or or_1 (Branch, Branch1, Branch2, Branch3, Branch4, Branch5, Branch6, Branch7);
  or or_2 (ALUSrc, ALUSrc1, ALUSrc2, ALUSrc3, ALUSrc4, ALUSrc5, ALUSrc6, ALUSrc7);
  or or_3 (RegDst, RegDst1, RegDst2, RegDst3, RegDst4, RegDst5, RegDst6, RegDst7);
  or or_4 (Lui, Lui1, Lui2, Lui3, Lui4, Lui5, Lui6, Lui7);
  or or_5 (jump, j1, j2, j3, j4, j5, j6, j7);
  or or_6 (REGorMEM, REGorMEM1, REGorMEM2, REGorMEM3, REGorMEM4, REGorMEM5, REGorMEM6, REGorMEM7);
  or or_7 (MemWrite, MemWrite1, MemWrite2, MemWrite3, MemWrite4, MemWrite5, MemWrite6, MemWrite7);
  or or_8 (RegWrite, RegWrite1, RegWrite2, RegWrite3, RegWrite4, RegWrite5, RegWrite6, RegWrite7);
  or or_9 (ZeroEXT, ZeroEXT1, ZeroEXT2, ZeroEXT3, ZeroEXT4, ZeroEXT5, ZeroEXT6, ZeroEXT7);
  assign ALUOp = ALUOp1 | ALUOp2 | ALUOp3 | ALUOp4 | ALUOp5 | ALUOp6 | ALUOp7;  // OR_Gate or_10, 3 bits wide

  // Other names for the same wires on the sheet: OP[5:0] = Opcode_5_0

  // Notes on the sheet:
  //   R指令
  //   beq
  //   j
  //   lw
  //   ori
  //   lui
  //   sw
endmodule

module ALUDecoder (
  input  [5:0] Funct,
  input  [2:0] ALUOp,
  output [3:0] ALUControl
);

  wire and_1_out, and_2_out, and_3_out, and_4_out, and_5_out, and_6_out, and_7_out, and_8_out,
       comparator_1_eq, comparator_2_eq, comparator_3_eq, comparator_4_eq, comparator_5_eq, comparator_6_eq,
       comparator_7_eq, comparator_8_eq, comparator_9_eq, comparator_10_eq, comparator_11_eq,
       comparator_12_eq, comparator_13_eq, comparator_14_eq, comparator_15_eq, comparator_16_eq,
       comparator_17_eq, comparator_18_eq, comparator_19_eq, comparator_20_eq, or_1_out, or_2_out, or_3_out,
       or_4_out;
  wire [3:0] ADD, AND, OR, SLL, SLT, SRA, SRL, SUB;

  // Probe on 6'b100011
  Comparator #(.width(3), .mode("unsigned")) comparator_1 (
    .a(ALUOp), .b(3'b010), .eq(comparator_1_eq));  // open: gt, lt
  Comparator #(.width(6), .mode("unsigned")) comparator_2 (
    .a(Funct), .b(6'b100001), .eq(comparator_2_eq));  // open: gt, lt
  // Probe on 6'b100001
  Comparator #(.width(3), .mode("unsigned")) comparator_3 (
    .a(ALUOp), .b(3'b010), .eq(comparator_3_eq));  // open: gt, lt
  Comparator #(.width(6), .mode("unsigned")) comparator_4 (
    .a(Funct), .b(6'b100011), .eq(comparator_4_eq));  // open: gt, lt
  Comparator #(.width(3), .mode("unsigned")) comparator_5 (
    .a(ALUOp), .b(3'b010), .eq(comparator_5_eq));  // open: gt, lt
  Comparator #(.width(6), .mode("unsigned")) comparator_6 (
    .a(Funct), .b(6'b100100), .eq(comparator_6_eq));  // open: gt, lt
  // Probe on 6'b100100
  Comparator #(.width(3), .mode("unsigned")) comparator_7 (
    .a(ALUOp), .b(3'b010), .eq(comparator_7_eq));  // open: gt, lt
  Comparator #(.width(6), .mode("unsigned")) comparator_8 (
    .a(Funct), .b(6'b100101), .eq(comparator_8_eq));  // open: gt, lt
  // Probe on 6'b100101
  Comparator #(.width(3), .mode("unsigned")) comparator_9 (
    .a(ALUOp), .b(3'b010), .eq(comparator_9_eq));  // open: gt, lt
  Comparator #(.width(6), .mode("unsigned")) comparator_10 (
    .a(Funct), .b(6'b101010), .eq(comparator_10_eq));  // open: gt, lt
  // Probe on 6'b101010
  Comparator #(.width(3), .mode("unsigned")) comparator_11 (
    .a(ALUOp), .b(3'b010), .eq(comparator_11_eq));  // open: gt, lt
  Comparator #(.width(6), .mode("unsigned")) comparator_12 (
    .a(Funct), .b({6{1'b0}}), .eq(comparator_12_eq));  // open: gt, lt
  // Probe on {6{1'b0}}
  Comparator #(.width(3), .mode("unsigned")) comparator_13 (
    .a(ALUOp), .b(3'b010), .eq(comparator_13_eq));  // open: gt, lt
  Comparator #(.width(6), .mode("unsigned")) comparator_14 (
    .a(Funct), .b(6'b000010), .eq(comparator_14_eq));  // open: gt, lt
  // Probe on 6'b000010
  Comparator #(.width(3), .mode("unsigned")) comparator_15 (
    .a(ALUOp), .b(3'b010), .eq(comparator_15_eq));  // open: gt, lt
  Comparator #(.width(6), .mode("unsigned")) comparator_16 (
    .a(Funct), .b(6'b000011), .eq(comparator_16_eq));  // open: gt, lt
  // Probe on 6'b000011
  Comparator #(.width(3), .mode("unsigned")) comparator_17 (
    .a(ALUOp), .b(3'b000), .eq(comparator_17_eq));  // open: gt, lt
  and and_1 (and_1_out, comparator_1_eq, comparator_2_eq);
  Comparator #(.width(3), .mode("unsigned")) comparator_18 (
    .a(ALUOp), .b(3'b001), .eq(comparator_18_eq));  // open: gt, lt
  and and_2 (and_2_out, comparator_3_eq, comparator_4_eq);
  Comparator #(.width(3), .mode("unsigned")) comparator_19 (
    .a(ALUOp), .b(3'b011), .eq(comparator_19_eq));  // open: gt, lt
  and and_3 (and_3_out, comparator_5_eq, comparator_6_eq);
  Comparator #(.width(3), .mode("unsigned")) comparator_20 (
    .a(ALUOp), .b(3'b100), .eq(comparator_20_eq));  // open: gt, lt
  and and_4 (and_4_out, comparator_7_eq, comparator_8_eq);
  and and_5 (and_5_out, comparator_9_eq, comparator_10_eq);
  and and_6 (and_6_out, comparator_11_eq, comparator_12_eq);
  and and_7 (and_7_out, comparator_13_eq, comparator_14_eq);
  and and_8 (and_8_out, comparator_15_eq, comparator_16_eq);
  or or_1 (or_1_out, comparator_17_eq, and_1_out);
  // Probe on 4'b0110
  or or_2 (or_2_out, comparator_18_eq, and_2_out);
  or or_3 (or_3_out, comparator_19_eq, and_3_out);
  or or_4 (or_4_out, comparator_20_eq, and_4_out);
  // Probe on 4'b0111
  Multiplexer #(.width(4), .enable("false")) multiplexer_1 (.in0(4'b0000), .in1(4'b0111), .out(SLT), .sel(and_5_out));
  // Probe on 4'b1000
  Multiplexer #(.width(4), .enable("false")) multiplexer_2 (.in0(4'b0000), .in1(4'b1000), .out(SLL), .sel(and_6_out));
  // Probe on 4'b1001
  Multiplexer #(.width(4), .enable("false")) multiplexer_3 (.in0(4'b0000), .in1(4'b1001), .out(SRL), .sel(and_7_out));
  // Probe on 4'b1010
  Multiplexer #(.width(4), .enable("false")) multiplexer_4 (.in0(4'b0000), .in1(4'b1010), .out(SRA), .sel(and_8_out));
  // Probe on ADD
  // Probe on 4'b0010
  Multiplexer #(.width(4), .enable("false")) multiplexer_5 (.in0(4'b0000), .in1(4'b0010), .out(ADD), .sel(or_1_out));
  // Probe on SUB
  Multiplexer #(.width(4), .enable("false")) multiplexer_6 (.in0(4'b0000), .in1(4'b0110), .out(SUB), .sel(or_2_out));
  // Probe on 4'b0000
  // Probe on AND
  Multiplexer #(.width(4), .enable("false")) multiplexer_7 (.in0(4'b0000), .in1(4'b0000), .out(AND), .sel(or_3_out));
  // Probe on OR
  // Probe on 4'b0001
  Multiplexer #(.width(4), .enable("false")) multiplexer_8 (.in0(4'b0000), .in1(4'b0001), .out(OR), .sel(or_4_out));
  // Probe on SLT
  // Probe on SLL
  // Probe on SRL
  // Probe on SRA
  assign ALUControl = ADD | SUB | AND | OR | SLT | SLL | SRL | SRA;  // OR_Gate or_5, 4 bits wide

  // Notes on the sheet:
  //   ADD
  //   SUB
  //   AND
  //   OR
  //   SLT
  //   SLL
  //   SRL
  //   SRA
endmodule
