// Logisim project p3_cpu_second - 异步复位至0x3000.circ as structural Verilog: 10 circuits, main circuit main
module main (
  input  rst,
  output [31:0] out_2,
  output out_3,
  output [4:0] out_4,
  output [31:0] out_5,
  output out_6,
  output [4:0] out_7,
  output [31:0] out_8
);

  wire A2op, ALU_Aop, ALUZero, clk, REGorMEM, ZeroEXT;
  wire [1:0] A1op, A3op, ALU_Bop, REGop;
  wire [2:0] NPCOp;
  wire [3:0] ALUOp;
  wire [4:0] multiplexer_1_out, multiplexer_2_out, rd, rs, rt, shamt;
  wire [5:0] funct, opcode;
  wire [15:0] _16imm;
  wire [25:0] _26imm;
  wire [31:0] dm_1_rd, ext_1_out_3, GPR_rs, MemAddr, multiplexer_5_out, multiplexer_6_out, multiplexer_7_out,
       new_pc_1_pc, npc_1_npc, pc_4, shamt32, shifter_1_out, shifter_2_out;

  Clock clock_1 (.out(clk));
  // Probe on npc_1_npc
  NPC npc_1 (
    ._26imm(_26imm), .ra(GPR_rs), .NPC(npc_1_npc), .NPCOp(NPCOp), .PC(new_pc_1_pc), .ALUZero(ALUZero),
    .PC_4(pc_4));
  // Probe on new_pc_1_pc
  new_pc new_pc_1 (.NPC(npc_1_npc), .PC(new_pc_1_pc), .CLK(clk), .RESET(rst));
  IM im_1 (.PC(new_pc_1_pc), .instr(out_2));
  splitter splitter_1 (
    .in_1(out_2), .rs(rs), .rt(rt), .rd(rd), .shamt(shamt), .opcode(opcode), .funct(funct),
    ._16bit_imm(_16imm), ._26bit_imm(_26imm));
  EXT ext_1 (.IMM(_16imm), .out_3(ext_1_out_3), .ZeroExt(ZeroEXT));
  assign shamt32 = {{27{1'b0}}, shamt};  // Bit_Extender bit_extender_1
  Multiplexer #(.select(2), .width(5), .enable("false")) multiplexer_1 (
    .in0(rs), .in1(rt), .out(multiplexer_1_out), .sel(A1op));  // open: in2, in3
  Shifter #(.width(32)) shifter_1 (.in(ext_1_out_3), .\dist (5'b10000), .out(shifter_1_out));
  Multiplexer #(.width(5), .enable("false")) multiplexer_2 (
    .in0(rt), .out(multiplexer_2_out), .sel(A2op));  // open: in1
  Multiplexer #(.select(2), .width(5), .enable("false")) multiplexer_3 (
    .in0(rd), .in1(rt), .in2({5{1'b1}}), .out(out_4), .sel(A3op));  // open: in3
  Controller controller_1 (
    .opcode(opcode), .funct(funct), .REGorMEM(REGorMEM), .MemWrite(out_6), .NPCop(NPCOp), .ZeroEXT(ZeroEXT),
    .A1op(A1op), .A2op(A2op), .A3op(A3op), .REGop(REGop), .RegWrite(out_3), .ALU_Aop(ALU_Aop),
    .ALU_Bop(ALU_Bop), .ALUOp(ALUOp));
  Multiplexer #(.select(2), .width(32), .enable("false")) multiplexer_4 (
    .in0(multiplexer_7_out), .in1(shifter_1_out), .in2(pc_4), .out(out_5), .sel(REGop));  // open: in3
  GRF grf_1 (
    .A1(multiplexer_1_out), .A2(multiplexer_2_out), .A3(out_4), .WD(out_5), .RD1(GPR_rs), .RD2(out_8),
    .CLK(clk), .RESET(rst), .WE(out_3));
  Multiplexer #(.width(32), .enable("false")) multiplexer_5 (
    .in0(GPR_rs), .out(multiplexer_5_out), .sel(ALU_Aop));  // open: in1
  Multiplexer #(.select(2), .width(32), .enable("false")) multiplexer_6 (
    .in0(out_8), .in1(ext_1_out_3), .in2(shamt32), .out(multiplexer_6_out), .sel(ALU_Bop));  // open: in3
  ALU alu_1 (.SrcA(multiplexer_5_out), .SrcB(multiplexer_6_out), .ALUZero(ALUZero), .ALUResult(MemAddr), .ALUOp(ALUOp));
  Bit_Extender #(.in_width(32), .out_width(5)) bit_extender_2 (.in(shifter_2_out), .out(out_7));
  Shifter #(.width(32), .shift("lr")) shifter_2 (.in(MemAddr), .\dist (5'b00010), .out(shifter_2_out));
  DM dm_1 (.A(MemAddr), .WD(out_8), .RD(dm_1_rd), .clk(clk), .in_2(out_6), .in_5(rst));
  Multiplexer #(.width(32), .enable("false")) multiplexer_7 (
    .in0(MemAddr), .in1(dm_1_rd), .out(multiplexer_7_out), .sel(REGorMEM));

  // Other names for the same wires on the sheet: instr[31:0] = out_2; MemWrite = out_6; RegAddr[4:0] = out_4;
  //   RegData[31:0] = out_5; RegWrite = out_3; WriteData[31:0] = out_8

  // Notes on the sheet:
  //   二战！！！
  //   instructions：addu，subu，ori，lw，sw，beq，lui，
  //   sll，srl，sra，slt，j，jal，jalr，jr，nop
endmodule

module IM (
  input  [31:0] PC,
  output [31:0] instr
);

  wire [4:0] bit_extender_1_out;
  wire [31:0] shifter_1_out;

  Shifter #(.width(32), .shift("lr")) shifter_1 (.in(PC), .\dist (5'b00010), .out(shifter_1_out));
  Bit_Extender #(.in_width(32), .out_width(5)) bit_extender_1 (.in(shifter_1_out), .out(bit_extender_1_out));
  ROM #(.addrWidth(5), .dataWidth(32)) rom_1 (.addr(bit_extender_1_out), .data(instr));  // open: sel
endmodule

module GRF (
  input  [4:0] A1,
  input  [4:0] A2,
  input  [4:0] A3,
  input  CLK,
  input  RESET,
  input  WE,
  input  [31:0] WD,
  output [31:0] RD1,
  output [31:0] RD2
);

  wire [31:0] IN_0, IN_1, IN_2, IN_3, IN_4, IN_5, IN_6, IN_7, IN_8, IN_9, IN_10, IN_11, IN_12, IN_13, IN_14,
       IN_15, IN_16, IN_17, IN_18, IN_19, IN_20, IN_21, IN_22, IN_23, IN_24, IN_25, IN_26, IN_27, IN_28,
       IN_29, IN_30, IN_31, OUT_0, OUT_1, OUT_2, OUT_3, OUT_4, OUT_5, OUT_6, OUT_7, OUT_8, OUT_9, OUT_10,
       OUT_11, OUT_12, OUT_13, OUT_14, OUT_15, OUT_16, OUT_17, OUT_18, OUT_19, OUT_20, OUT_21, OUT_22,
       OUT_23, OUT_24, OUT_25, OUT_26, OUT_27, OUT_28, OUT_29, OUT_30, OUT_31;

  // Probe on A1
  // Probe on A2
  // Probe on A3
  Demultiplexer #(.select(5), .width(32), .tristate("true")) demultiplexer_1 (
    .out0(IN_0), .out1(IN_1), .out2(IN_2), .out3(IN_3), .out4(IN_4), .out5(IN_5), .out6(IN_6), .out7(IN_7),
    .out8(IN_8), .out9(IN_9), .out10(IN_10), .out11(IN_11), .out12(IN_12), .out13(IN_13), .out14(IN_14),
    .out15(IN_15), .out16(IN_16), .out17(IN_17), .out18(IN_18), .out19(IN_19), .out20(IN_20), .out21(IN_21),
    .out22(IN_22), .out23(IN_23), .out24(IN_24), .out25(IN_25), .out26(IN_26), .out27(IN_27), .out28(IN_28),
    .out29(IN_29), .out30(IN_30), .out31(IN_31), .in(WD), .sel(A3));  // open: en
  // Probe on WD
  Multiplexer #(.select(5), .width(32)) multiplexer_1 (
    .in0(OUT_0), .in1(OUT_1), .in2(OUT_2), .in3(OUT_3), .in4(OUT_4), .in5(OUT_5), .in6(OUT_6), .in7(OUT_7),
    .in8(OUT_8), .in9(OUT_9), .in10(OUT_10), .in11(OUT_11), .in12(OUT_12), .in13(OUT_13), .in14(OUT_14),
    .in15(OUT_15), .in16(OUT_16), .in17(OUT_17), .in18(OUT_18), .in19(OUT_19), .in20(OUT_20), .in21(OUT_21),
    .in22(OUT_22), .in23(OUT_23), .in24(OUT_24), .in25(OUT_25), .in26(OUT_26), .in27(OUT_27), .in28(OUT_28),
    .in29(OUT_29), .in30(OUT_30), .in31(OUT_31), .out(RD1), .sel(A1));  // open: en
  Multiplexer #(.select(5), .width(32)) multiplexer_2 (
    .in0(OUT_0), .in1(OUT_1), .in2(OUT_2), .in3(OUT_3), .in4(OUT_4), .in5(OUT_5), .in6(OUT_6), .in7(OUT_7),
    .in8(OUT_8), .in9(OUT_9), .in10(OUT_10), .in11(OUT_11), .in12(OUT_12), .in13(OUT_13), .in14(OUT_14),
    .in15(OUT_15), .in16(OUT_16), .in17(OUT_17), .in18(OUT_18), .in19(OUT_19), .in20(OUT_20), .in21(OUT_21),
    .in22(OUT_22), .in23(OUT_23), .in24(OUT_24), .in25(OUT_25), .in26(OUT_26), .in27(OUT_27), .in28(OUT_28),
    .in29(OUT_29), .in30(OUT_30), .in31(OUT_31), .out(RD2), .sel(A2));  // open: en
  Register #(.width(32)) NO_0 (.D(IN_0), .en(WE), .Q(OUT_0), .clk(CLK), .clr(1'b1));
  Register #(.width(32)) NO_4 (.D(IN_4), .en(WE), .Q(OUT_4), .clk(CLK), .clr(RESET));
  Register #(.width(32)) NO_8 (.D(IN_8), .en(WE), .Q(OUT_8), .clk(CLK), .clr(RESET));
  Register #(.width(32)) NO_12 (.D(IN_12), .en(WE), .Q(OUT_12), .clk(CLK), .clr(RESET));
  Register #(.width(32)) NO_16 (.D(IN_16), .en(WE), .Q(OUT_16), .clk(CLK), .clr(RESET));
  Register #(.width(32)) NO_20 (.D(IN_20), .en(WE), .Q(OUT_20), .clk(CLK), .clr(RESET));
  Register #(.width(32)) NO_24 (.D(IN_24), .en(WE), .Q(OUT_24), .clk(CLK), .clr(RESET));
  Register #(.width(32)) NO_28 (.D(IN_28), .en(WE), .Q(OUT_28), .clk(CLK), .clr(RESET));
  Register #(.width(32)) NO_1 (.D(IN_1), .en(WE), .Q(OUT_1), .clk(CLK), .clr(RESET));
  Register #(.width(32)) NO_5 (.D(IN_5), .en(WE), .Q(OUT_5), .clk(CLK), .clr(RESET));
  Register #(.width(32)) NO_9 (.D(IN_9), .en(WE), .Q(OUT_9), .clk(CLK), .clr(RESET));
  Register #(.width(32)) NO_13 (.D(IN_13), .en(WE), .Q(OUT_13), .clk(CLK), .clr(RESET));
  Register #(.width(32)) NO_17 (.D(IN_17), .en(WE), .Q(OUT_17), .clk(CLK), .clr(RESET));
  Register #(.width(32)) NO_21 (.D(IN_21), .en(WE), .Q(OUT_21), .clk(CLK), .clr(RESET));
  Register #(.width(32)) NO_25 (.D(IN_25), .en(WE), .Q(OUT_25), .clk(CLK), .clr(RESET));
  Register #(.width(32)) NO_29 (.D(IN_29), .en(WE), .Q(OUT_29), .clk(CLK), .clr(RESET));
  Register #(.width(32)) NO_2 (.D(IN_2), .en(WE), .Q(OUT_2), .clk(CLK), .clr(RESET));
  Register #(.width(32)) NO_6 (.D(IN_6), .en(WE), .Q(OUT_6), .clk(CLK), .clr(RESET));
  Register #(.width(32)) NO_10 (.D(IN_10), .en(WE), .Q(OUT_10), .clk(CLK), .clr(RESET));
  Register #(.width(32)) NO_14 (.D(IN_14), .en(WE), .Q(OUT_14), .clk(CLK), .clr(RESET));
  Register #(.width(32)) NO_18 (.D(IN_18), .en(WE), .Q(OUT_18), .clk(CLK), .clr(RESET));
  Register #(.width(32)) NO_22 (.D(IN_22), .en(WE), .Q(OUT_22), .clk(CLK), .clr(RESET));
  Register #(.width(32)) NO_26 (.D(IN_26), .en(WE), .Q(OUT_26), .clk(CLK), .clr(RESET));
  Register #(.width(32)) NO_30 (.D(IN_30), .en(WE), .Q(OUT_30), .clk(CLK), .clr(RESET));
  Register #(.width(32)) NO_3 (.D(IN_3), .en(WE), .Q(OUT_3), .clk(CLK), .clr(RESET));
  Register #(.width(32)) NO_7 (.D(IN_7), .en(WE), .Q(OUT_7), .clk(CLK), .clr(RESET));
  Register #(.width(32)) NO_11 (.D(IN_11), .en(WE), .Q(OUT_11), .clk(CLK), .clr(RESET));
  Register #(.width(32)) NO_15 (.D(IN_15), .en(WE), .Q(OUT_15), .clk(CLK), .clr(RESET));
  Register #(.width(32)) NO_19 (.D(IN_19), .en(WE), .Q(OUT_19), .clk(CLK), .clr(RESET));
  Register #(.width(32)) NO_23 (.D(IN_23), .en(WE), .Q(OUT_23), .clk(CLK), .clr(RESET));
  Register #(.width(32)) NO_27 (.D(IN_27), .en(WE), .Q(OUT_27), .clk(CLK), .clr(RESET));
  Register #(.width(32)) NO_31 (.D(IN_31), .en(WE), .Q(OUT_31), .clk(CLK), .clr(RESET));

  // Other names for the same wires on the sheet: out_address1[31:0] = RD1; out_address2[31:0] = RD2;
  //   read_address1[4:0] = A1; read_address2[4:0] = A2; write_address[4:0] = A3; write_data[31:0] = WD;
  //   write_enable = WE
endmodule

module splitter (
  input  [31:0] in_1,
  output [5:0] opcode,
  output [5:0] funct,
  output [4:0] rs,
  output [4:0] rt,
  output [4:0] rd,
  output [4:0] shamt,
  output [25:0] _26bit_imm,
  output [15:0] _16bit_imm
);


  assign _16bit_imm = in_1[15:0];
  assign _26bit_imm = in_1[25:0];
  assign funct = in_1[5:0];
  assign opcode = in_1[31:26];
  assign rd = in_1[15:11];
  assign rs = in_1[25:21];
  assign rt = in_1[20:16];
  assign shamt = in_1[10:6];
endmodule

module ALU (
  input  [3:0] ALUOp,
  input  [31:0] SrcA,
  input  [31:0] SrcB,
  output ALUZero,
  output [31:0] ALUResult
);

  wire comparator_1_eq, comparator_2_eq, comparator_3_eq, comparator_4_eq, comparator_5_lt, comparator_6_eq,
       comparator_7_eq, comparator_9_eq, comparator_10_eq;
  wire [4:0] bit_extender_1_out, bit_extender_2_out, bit_extender_4_out;
  wire [31:0] ADD, adder_1_out, adder_2_out, AND, and_1_out, bit_extender_3_out, not_1_out, OR, or_1_out,
       shifter_1_out, shifter_2_out, shifter_3_out, SLL, SLT, SRA, SRL, SUB;

  // Probe on 4'b0000
  assign not_1_out = ~SrcB;  // NOT_Gate not_1, 32 bits wide
  // Probe on 4'b0011
  Bit_Extender #(.in_width(32), .out_width(5)) bit_extender_1 (.in(SrcB), .out(bit_extender_1_out));
  // Probe on 4'b0110
  assign and_1_out = SrcA & SrcB;  // AND_Gate and_1, 32 bits wide
  Comparator #(.width(4), .mode("unsigned")) comparator_1 (
    .a(ALUOp), .b(4'b0000), .eq(comparator_1_eq));  // open: gt, lt
  Adder #(.width(32)) adder_1 (.a(SrcA), .b(not_1_out), .out(adder_1_out), .cin(1'b1));  // open: cout
  Comparator #(.width(4), .mode("unsigned")) comparator_2 (
    .a(ALUOp), .b(4'b0011), .eq(comparator_2_eq));  // open: gt, lt
  Shifter #(.width(32), .shift("ar")) shifter_1 (.in(SrcA), .\dist (bit_extender_1_out), .out(shifter_1_out));
  Comparator #(.width(4), .mode("unsigned")) comparator_3 (
    .a(ALUOp), .b(4'b0110), .eq(comparator_3_eq));  // open: gt, lt
  Multiplexer #(.width(32), .enable("false")) multiplexer_1 (
    .in0({32{1'b0}}), .in1(and_1_out), .out(AND), .sel(comparator_1_eq));
  Multiplexer #(.width(32), .enable("false")) multiplexer_2 (
    .in0({32{1'b0}}), .in1(adder_1_out), .out(SUB), .sel(comparator_2_eq));
  Multiplexer #(.width(32), .enable("false")) multiplexer_3 (
    .in0({32{1'b0}}), .in1(shifter_1_out), .out(SRA), .sel(comparator_3_eq));
  assign or_1_out = SrcA | SrcB;  // OR_Gate or_1, 32 bits wide
  Comparator #(.width(4), .mode("unsigned")) comparator_4 (
    .a(ALUOp), .b(4'b0001), .eq(comparator_4_eq));  // open: gt, lt
  // Probe on 4'b0001
  Bit_Extender #(.in_width(32), .out_width(5)) bit_extender_2 (.in(SrcB), .out(bit_extender_2_out));
  // Probe on 4'b0100
  Comparator #(.width(32)) comparator_5 (.a(SrcA), .b(SrcB), .lt(comparator_5_lt));  // open: gt, eq
  // Probe on 4'b0111
  Multiplexer #(.width(32), .enable("false")) multiplexer_4 (
    .in0({32{1'b0}}), .in1(or_1_out), .out(OR), .sel(comparator_4_eq));
  Multiplexer #(.width(32), .enable("false")) multiplexer_5 (
    .in0({32{1'b0}}), .in1(shifter_2_out), .out(SLL), .sel(comparator_6_eq));
  Shifter #(.width(32)) shifter_2 (.in(SrcA), .\dist (bit_extender_2_out), .out(shifter_2_out));
  Comparator #(.width(4), .mode("unsigned")) comparator_6 (
    .a(ALUOp), .b(4'b0100), .eq(comparator_6_eq));  // open: gt, lt
  Multiplexer #(.width(32), .enable("false")) multiplexer_6 (
    .in0({32{1'b0}}), .in1(bit_extender_3_out), .out(SLT), .sel(comparator_7_eq));
  assign bit_extender_3_out = {{31{1'b0}}, comparator_5_lt};  // Bit_Extender bit_extender_3
  Comparator #(.width(4), .mode("unsigned")) comparator_7 (
    .a(ALUOp), .b(4'b0111), .eq(comparator_7_eq));  // open: gt, lt
  Comparator #(.width(32)) comparator_8 (.a(SrcA), .b(SrcB), .eq(ALUZero));  // open: gt, lt
  // Probe on 4'b0010
  Bit_Extender #(.in_width(32), .out_width(5)) bit_extender_4 (.in(SrcB), .out(bit_extender_4_out));
  // Probe on 4'b0101
  assign ALUResult = AND | OR | ADD | SUB | SLL | SRL | SRA | SLT;  // OR_Gate or_2, 32 bits wide
  Multiplexer #(.width(32), .enable("false")) multiplexer_7 (
    .in0({32{1'b0}}), .in1(adder_2_out), .out(ADD), .sel(comparator_9_eq));
  Adder #(.width(32)) adder_2 (.a(SrcA), .b(SrcB), .out(adder_2_out));  // open: cin, cout
  Comparator #(.width(4), .mode("unsigned")) comparator_9 (
    .a(ALUOp), .b(4'b0010), .eq(comparator_9_eq));  // open: gt, lt
  Multiplexer #(.width(32), .enable("false")) multiplexer_8 (
    .in0({32{1'b0}}), .in1(shifter_3_out), .out(SRL), .sel(comparator_10_eq));
  Shifter #(.width(32), .shift("lr")) shifter_3 (.in(SrcA), .\dist (bit_extender_4_out), .out(shifter_3_out));
  Comparator #(.width(4), .mode("unsigned")) comparator_10 (
    .a(ALUOp), .b(4'b0101), .eq(comparator_10_eq));  // open: gt, lt

  // Notes on the sheet:
  //   注：SLT有符号！！！！！！
  //   SLTU才是无符号
endmodule

module DM (
  input  clk,
  input  in_2,
  input  [31:0] A,
  input  [31:0] WD,
  input  in_5,
  output [31:0] RD
);

  wire [4:0] bit_extender_1_out;
  wire [31:0] shifter_1_out;

  Shifter #(.width(32), .shift("lr")) shifter_1 (.in(A), .\dist (5'b00010), .out(shifter_1_out));
  // Probe on shifter_1_out
  Bit_Extender #(.in_width(32), .out_width(5)) bit_extender_1 (.in(shifter_1_out), .out(bit_extender_1_out));
  // Probe on WD
  // Probe on bit_extender_1_out
  RAM #(.addrWidth(5), .dataWidth(32), .bus("separate")) ram_1 (
    .addr(bit_extender_1_out), .din(WD), .data(RD), .str(in_2), .clk(clk), .clr(in_5));  // open: sel, ld

  // Other names for the same wires on the sheet: rst = in_5; WE = in_2
endmodule

module EXT (
  input  ZeroExt,
  input  [15:0] IMM,
  output [31:0] out_3
);

  wire [31:0] bit_extender_1_out, bit_extender_2_out;

  assign bit_extender_1_out = {{16{IMM[15]}}, IMM};  // Bit_Extender bit_extender_1
  Multiplexer #(.width(32), .enable("false")) multiplexer_1 (
    .in0(bit_extender_1_out), .in1(bit_extender_2_out), .out(out_3), .sel(ZeroExt));
  assign bit_extender_2_out = {{16{1'b0}}, IMM};  // Bit_Extender bit_extender_2

  // Other names for the same wires on the sheet: zero_ext = ZeroExt
endmodule

module NPC (
  input  [2:0] NPCOp,
  input  [31:0] PC,
  input  [31:0] ra,
  input  [25:0] _26imm,
  input  ALUZero,
  output [31:0] NPC,
  output [31:0] PC_4
);

  wire [15:0] _16imm;
  wire [31:0] adder_1_out, adder_2_out, bit_extender_1_out, multiplexer_1_out, shifter_1_out;

  assign bit_extender_1_out = {{16{_16imm[15]}}, _16imm};  // Bit_Extender bit_extender_1
  Bit_Extender #(.in_width(26)) bit_extender_2 (.in(_26imm), .out(_16imm));
  Shifter #(.width(32)) shifter_1 (.in(bit_extender_1_out), .\dist (5'b00010), .out(shifter_1_out));
  Multiplexer #(.width(32), .enable("false")) multiplexer_1 (
    .in0({32{1'b0}}), .in1(shifter_1_out), .out(multiplexer_1_out), .sel(ALUZero));
  // Probe on {PC[31:28], _26imm, 2'b00}
  Adder #(.width(32)) adder_1 (.a(PC), .b(32'h4), .out(adder_1_out));  // open: cin, cout
  Adder #(.width(32)) adder_2 (.a(adder_1_out), .b(multiplexer_1_out), .out(adder_2_out));  // open: cin, cout
  Multiplexer #(.select(3), .width(32), .enable("false")) multiplexer_2 (
    .in0(adder_1_out), .in1(adder_2_out), .in2({PC[31:28], _26imm, 2'b00}), .in3(ra), .out(NPC), .sel(NPCOp));  // open: in4, in5, in6, in7
  Adder #(.width(32)) adder_3 (.a(PC), .b(32'h4), .out(PC_4));  // open: cin, cout

  // Other names for the same wires on the sheet: PC_31_28[3:0] = PC[31:28]

  // Notes on the sheet:
  //   000：PC + 4
  //   001：beq（需结合ALUZero判断
  //   010：跳转26位立即数
  //   011：跳转$ra寄存器
endmodule

module Controller (
  input  [5:0] opcode,
  input  [5:0] funct,
  output REGorMEM,
  output MemWrite,
  output [2:0] NPCop,
  output ZeroEXT,
  output [1:0] A1op,
  output A2op,
  output [1:0] A3op,
  output [1:0] REGop,
  output RegWrite,
  output ALU_Aop,
  output [1:0] ALU_Bop,
  output [3:0] ALUOp
);

  wire A2op1, A2op2, A2op3, A2op4, A2op5, A2op6, A2op7, A2op8, A2op9, A2op10, A2op11, A2op12, A2op13, A2op14,
       A2op15, A2op16, ALU_Aop1, ALU_Aop2, ALU_Aop3, ALU_Aop4, ALU_Aop5, ALU_Aop6, ALU_Aop7, ALU_Aop8,
       ALU_Aop9, ALU_Aop10, ALU_Aop11, ALU_Aop12, ALU_Aop13, ALU_Aop14, ALU_Aop15, ALU_Aop16, and_1_out,
       and_2_out, and_3_out, and_4_out, and_5_out, and_6_out, and_7_out, and_8_out, and_9_out,
       comparator_1_eq, comparator_2_eq, comparator_3_eq, comparator_4_eq, comparator_5_eq, comparator_6_eq,
       comparator_7_eq, comparator_8_eq, comparator_9_eq, comparator_10_eq, comparator_11_eq,
       comparator_12_eq, comparator_13_eq, comparator_14_eq, comparator_15_eq, comparator_16_eq,
       comparator_17_eq, comparator_18_eq, comparator_19_eq, comparator_20_eq, comparator_21_eq,
       comparator_22_eq, comparator_23_eq, comparator_24_eq, comparator_25_eq, MemWrite1, MemWrite2,
       MemWrite3, MemWrite4, MemWrite5, MemWrite6, MemWrite7, MemWrite8, MemWrite9, MemWrite10, MemWrite11,
       MemWrite12, MemWrite13, MemWrite14, MemWrite15, MemWrite16, REGorMEM1, REGorMEM2, REGorMEM3,
       REGorMEM4, REGorMEM5, REGorMEM6, REGorMEM7, REGorMEM8, REGorMEM9, REGorMEM10, REGorMEM11, REGorMEM12,
       REGorMEM13, REGorMEM14, REGorMEM15, REGorMEM16, RegWrite1, RegWrite2, RegWrite3, RegWrite4, RegWrite5,
       RegWrite6, RegWrite7, RegWrite8, RegWrite9, RegWrite10, RegWrite11, RegWrite12, RegWrite13,
       RegWrite14, RegWrite15, RegWrite16, undriven, ZeroEXT1, ZeroEXT2, ZeroEXT3, ZeroEXT4, ZeroEXT5,
       ZeroEXT6, ZeroEXT7, ZeroEXT8, ZeroEXT9, ZeroEXT10, ZeroEXT11, ZeroEXT12, ZeroEXT13, ZeroEXT14,
       ZeroEXT15, ZeroEXT16;
  wire [1:0] A1op1, A1op2, A1op3, A1op4, A1op5, A1op6, A1op7, A1op8, A1op9, A1op10, A1op11, A1op12, A1op13,
       A1op14, A1op15, A1op16, A3op1, A3op2, A3op3, A3op4, A3op5, A3op6, A3op7, A3op8, A3op9, A3op10, A3op11,
       A3op12, A3op13, A3op14, A3op15, A3op16, ALU_Bop1, ALU_Bop2, ALU_Bop3, ALU_Bop4, ALU_Bop5, ALU_Bop6,
       ALU_Bop7, ALU_Bop8, ALU_Bop9, ALU_Bop10, ALU_Bop11, ALU_Bop12, ALU_Bop13, ALU_Bop14, ALU_Bop15,
       ALU_Bop16, REGop1, REGop2, REGop3, REGop4, REGop5, REGop6, REGop7, REGop8, REGop9, REGop10, REGop11,
       REGop12, REGop13, REGop14, REGop15, REGop16;
  wire [2:0] NPCop1, NPCop2, NPCop3, NPCop4, NPCop5, NPCop6, NPCop7, NPCop8, NPCop9, NPCop10, NPCop11,
       NPCop12, NPCop13, NPCop14, NPCop15, NPCop16;
  wire [3:0] ALUOp1, ALUOp2, ALUOp3, ALUOp4, ALUOp5, ALUOp6, ALUOp7, ALUOp8, ALUOp9, ALUOp10, ALUOp11,
       ALUOp12, ALUOp13, ALUOp14, ALUOp15, ALUOp16;

  Comparator #(.width(6), .mode("unsigned")) comparator_1 (
    .a(funct), .b(6'b100001), .eq(comparator_1_eq));  // open: gt, lt
  // Probe on 6'b100001
  Comparator #(.width(6), .mode("unsigned")) comparator_2 (
    .a(opcode), .b({6{1'b0}}), .eq(comparator_2_eq));  // open: gt, lt
  // Probe on {6{1'b0}}
  // Probe on 6'b000010
  // Probe on {6{1'b0}}
  Comparator #(.width(6), .mode("unsigned")) comparator_3 (
    .a(funct), .b(6'b000010), .eq(comparator_3_eq));  // open: gt, lt
  Comparator #(.width(6), .mode("unsigned")) comparator_4 (
    .a(opcode), .b({6{1'b0}}), .eq(comparator_4_eq));  // open: gt, lt
  and and_1 (and_1_out, comparator_1_eq, comparator_2_eq);
  // Probe on 4'b0010
  and and_2 (and_2_out, comparator_3_eq, comparator_4_eq);
  Multiplexer #(.enable("false")) multiplexer_1 (.in0(1'b0), .in1(1'b0), .out(REGorMEM1), .sel(and_1_out));
  Multiplexer #(.enable("false")) multiplexer_2 (.in0(1'b0), .in1(1'b0), .out(MemWrite1), .sel(and_1_out));
  Multiplexer #(.width(3), .enable("false")) multiplexer_3 (.in0(3'b000), .in1(3'b000), .out(NPCop1), .sel(and_1_out));
  Multiplexer #(.enable("false")) multiplexer_4 (.in0(1'b0), .in1(1'b0), .out(ZeroEXT1), .sel(and_1_out));
  Multiplexer #(.width(2), .enable("false")) multiplexer_5 (.in0(2'b00), .in1(2'b00), .out(A1op1), .sel(and_1_out));
  Multiplexer #(.enable("false")) multiplexer_6 (.in0(1'b0), .in1(1'b0), .out(A2op1), .sel(and_1_out));
  Multiplexer #(.width(2), .enable("false")) multiplexer_7 (.in0(2'b00), .in1(2'b00), .out(A3op1), .sel(and_1_out));
  Multiplexer #(.width(2), .enable("false")) multiplexer_8 (.in0(2'b00), .in1(2'b00), .out(REGop1), .sel(and_1_out));
  Multiplexer #(.enable("false")) multiplexer_9 (.in0(1'b0), .in1(1'b1), .out(RegWrite1), .sel(and_1_out));
  Multiplexer #(.enable("false")) multiplexer_10 (.in0(1'b0), .in1(1'b0), .out(ALU_Aop1), .sel(and_1_out));
  Multiplexer #(.width(2), .enable("false")) multiplexer_11 (.in0(2'b00), .in1(2'b00), .out(ALU_Bop1), .sel(and_1_out));
  Multiplexer #(.width(4), .enable("false")) multiplexer_12 (
    .in0(4'b0000), .in1(4'b0010), .out(ALUOp1), .sel(and_1_out));
  Multiplexer #(.enable("false")) multiplexer_13 (.in0(1'b0), .in1(1'b0), .out(REGorMEM9), .sel(and_2_out));
  Multiplexer #(.enable("false")) multiplexer_14 (.in0(1'b0), .in1(1'b0), .out(MemWrite9), .sel(and_2_out));
  Multiplexer #(.width(3), .enable("false")) multiplexer_15 (.in0(3'b000), .in1(3'b000), .out(NPCop9), .sel(and_2_out));
  Multiplexer #(.enable("false")) multiplexer_16 (.in0(1'b0), .in1(1'b0), .out(ZeroEXT9), .sel(and_2_out));
  Multiplexer #(.width(2), .enable("false")) multiplexer_17 (.in0(2'b00), .in1(2'b01), .out(A1op9), .sel(and_2_out));
  Multiplexer #(.enable("false")) multiplexer_18 (.in0(1'b0), .in1(1'b0), .out(A2op9), .sel(and_2_out));
  Multiplexer #(.width(2), .enable("false")) multiplexer_19 (.in0(2'b00), .in1(2'b00), .out(A3op9), .sel(and_2_out));
  Multiplexer #(.width(2), .enable("false")) multiplexer_20 (.in0(2'b00), .in1(2'b00), .out(REGop9), .sel(and_2_out));
  Multiplexer #(.enable("false")) multiplexer_21 (.in0(1'b0), .in1(1'b1), .out(RegWrite9), .sel(and_2_out));
  Multiplexer #(.enable("false")) multiplexer_22 (.in0(1'b0), .in1(1'b0), .out(ALU_Aop9), .sel(and_2_out));
  Multiplexer #(.width(2), .enable("false")) multiplexer_23 (.in0(2'b00), .in1(2'b10), .out(ALU_Bop9), .sel(and_2_out));
  Multiplexer #(.width(4), .enable("false")) multiplexer_24 (
    .in0(4'b0000), .in1(4'b0101), .out(ALUOp9), .sel(and_2_out));
  // Probe on 4'b0101
  // Probe on 6'b100011
  // Probe on {6{1'b0}}
  // Probe on 6'b000011
  // Probe on {6{1'b0}}
  Comparator #(.width(6), .mode("unsigned")) comparator_5 (
    .a(funct), .b(6'b100011), .eq(comparator_5_eq));  // open: gt, lt
  Comparator #(.width(6), .mode("unsigned")) comparator_6 (
    .a(opcode), .b({6{1'b0}}), .eq(comparator_6_eq));  // open: gt, lt
  Comparator #(.width(6), .mode("unsigned")) comparator_7 (
    .a(funct), .b(6'b000011), .eq(comparator_7_eq));  // open: gt, lt
  Comparator #(.width(6), .mode("unsigned")) comparator_8 (
    .a(opcode), .b({6{1'b0}}), .eq(comparator_8_eq));  // open: gt, lt
  and and_3 (and_3_out, comparator_5_eq, comparator_6_eq);
  and and_4 (and_4_out, comparator_7_eq, comparator_8_eq);
  Multiplexer #(.enable("false")) multiplexer_25 (.in0(1'b0), .in1(1'b0), .out(REGorMEM2), .sel(and_3_out));
  Multiplexer #(.enable("false")) multiplexer_26 (.in0(1'b0), .in1(1'b0), .out(MemWrite2), .sel(and_3_out));
  Multiplexer #(.width(3), .enable("false")) multiplexer_27 (.in0(3'b000), .in1(3'b000), .out(NPCop2), .sel(and_3_out));
  Multiplexer #(.enable("false")) multiplexer_28 (.in0(1'b0), .in1(1'b0), .out(ZeroEXT2), .sel(and_3_out));
  Multiplexer #(.width(2), .enable("false")) multiplexer_29 (.in0(2'b00), .in1(2'b00), .out(A1op2), .sel(and_3_out));
  Multiplexer #(.enable("false")) multiplexer_30 (.in0(1'b0), .in1(1'b0), .out(A2op2), .sel(and_3_out));
  Multiplexer #(.width(2), .enable("false")) multiplexer_31 (.in0(2'b00), .in1(2'b00), .out(A3op2), .sel(and_3_out));
  Multiplexer #(.width(2), .enable("false")) multiplexer_32 (.in0(2'b00), .in1(2'b00), .out(REGop2), .sel(and_3_out));
  Multiplexer #(.enable("false")) multiplexer_33 (.in0(1'b0), .in1(1'b1), .out(RegWrite2), .sel(and_3_out));
  Multiplexer #(.enable("false")) multiplexer_34 (.in0(1'b0), .in1(1'b0), .out(ALU_Aop2), .sel(and_3_out));
  Multiplexer #(.width(2), .enable("false")) multiplexer_35 (.in0(2'b00), .in1(2'b00), .out(ALU_Bop2), .sel(and_3_out));
  Multiplexer #(.width(4), .enable("false")) multiplexer_36 (
    .in0(4'b0000), .in1(4'b0011), .out(ALUOp2), .sel(and_3_out));
  // Probe on 4'b0011
  Multiplexer #(.enable("false")) multiplexer_37 (.in0(1'b0), .in1(1'b0), .out(REGorMEM10), .sel(and_4_out));
  Multiplexer #(.enable("false")) multiplexer_38 (.in0(1'b0), .in1(1'b0), .out(MemWrite10), .sel(and_4_out));
  Multiplexer #(.width(3), .enable("false")) multiplexer_39 (
    .in0(3'b000), .in1(3'b000), .out(NPCop10), .sel(and_4_out));
  Multiplexer #(.enable("false")) multiplexer_40 (.in0(1'b0), .in1(1'b0), .out(ZeroEXT10), .sel(and_4_out));
  Multiplexer #(.width(2), .enable("false")) multiplexer_41 (.in0(2'b00), .in1(2'b01), .out(A1op10), .sel(and_4_out));
  Multiplexer #(.enable("false")) multiplexer_42 (.in0(1'b0), .in1(1'b0), .out(A2op10), .sel(and_4_out));
  Multiplexer #(.width(2), .enable("false")) multiplexer_43 (.in0(2'b00), .in1(2'b00), .out(A3op10), .sel(and_4_out));
  Multiplexer #(.width(2), .enable("false")) multiplexer_44 (.in0(2'b00), .in1(2'b00), .out(REGop10), .sel(and_4_out));
  Multiplexer #(.enable("false")) multiplexer_45 (.in0(1'b0), .in1(1'b1), .out(RegWrite10), .sel(and_4_out));
  Multiplexer #(.enable("false")) multiplexer_46 (.in0(1'b0), .in1(1'b0), .out(ALU_Aop10), .sel(and_4_out));
  Multiplexer #(.width(2), .enable("false")) multiplexer_47 (
    .in0(2'b00), .in1(2'b10), .out(ALU_Bop10), .sel(and_4_out));
  Multiplexer #(.width(4), .enable("false")) multiplexer_48 (
    .in0(4'b0000), .in1(4'b0110), .out(ALUOp10), .sel(and_4_out));
  // Probe on 4'b0110
  // Probe on 6'b101010
  // Probe on {6{1'b0}}
  // Probe on 6'b001101
  Comparator #(.width(6), .mode("unsigned")) comparator_9 (
    .a(funct), .b(6'b101010), .eq(comparator_9_eq));  // open: gt, lt
  Comparator #(.width(6), .mode("unsigned")) comparator_10 (
    .a(opcode), .b({6{1'b0}}), .eq(comparator_10_eq));  // open: gt, lt
  Comparator #(.width(6), .mode("unsigned")) comparator_11 (
    .a(opcode), .b(6'b001101), .eq(comparator_11_eq));  // open: gt, lt
  and and_5 (and_5_out, comparator_9_eq, comparator_10_eq);
  Multiplexer #(.enable("false")) multiplexer_49 (.in0(1'b0), .in1(1'b0), .out(REGorMEM3), .sel(comparator_11_eq));
  Multiplexer #(.enable("false")) multiplexer_50 (.in0(1'b0), .in1(1'b0), .out(MemWrite3), .sel(comparator_11_eq));
  Multiplexer #(.width(3), .enable("false")) multiplexer_51 (
    .in0(3'b000), .in1(3'b000), .out(NPCop3), .sel(comparator_11_eq));
  Multiplexer #(.enable("false")) multiplexer_52 (.in0(1'b0), .in1(1'b1), .out(ZeroEXT3), .sel(comparator_11_eq));
  Multiplexer #(.width(2), .enable("false")) multiplexer_53 (
    .in0(2'b00), .in1(2'b00), .out(A1op3), .sel(comparator_11_eq));
  Multiplexer #(.enable("false")) multiplexer_54 (.in0(1'b0), .in1(1'b0), .out(A2op3), .sel(comparator_11_eq));
  Multiplexer #(.width(2), .enable("false")) multiplexer_55 (
    .in0(2'b00), .in1(2'b01), .out(A3op3), .sel(comparator_11_eq));
  Multiplexer #(.width(2), .enable("false")) multiplexer_56 (
    .in0(2'b00), .in1(2'b00), .out(REGop3), .sel(comparator_11_eq));
  Multiplexer #(.enable("false")) multiplexer_57 (.in0(1'b0), .in1(1'b1), .out(RegWrite3), .sel(comparator_11_eq));
  Multiplexer #(.enable("false")) multiplexer_58 (.in0(1'b0), .in1(1'b0), .out(ALU_Aop3), .sel(comparator_11_eq));
  Multiplexer #(.width(2), .enable("false")) multiplexer_59 (
    .in0(2'b00), .in1(2'b01), .out(ALU_Bop3), .sel(comparator_11_eq));
  Multiplexer #(.width(4), .enable("false")) multiplexer_60 (
    .in0(4'b0000), .in1(4'b0001), .out(ALUOp3), .sel(comparator_11_eq));
  // Probe on 4'b0001
  Multiplexer #(.enable("false")) multiplexer_61 (.in0(1'b0), .in1(1'b0), .out(REGorMEM11), .sel(and_5_out));
  Multiplexer #(.enable("false")) multiplexer_62 (.in0(1'b0), .in1(1'b0), .out(MemWrite11), .sel(and_5_out));
  Multiplexer #(.width(3), .enable("false")) multiplexer_63 (
    .in0(3'b000), .in1(3'b000), .out(NPCop11), .sel(and_5_out));
  Multiplexer #(.enable("false")) multiplexer_64 (.in0(1'b0), .in1(1'b0), .out(ZeroEXT11), .sel(and_5_out));
  Multiplexer #(.width(2), .enable("false")) multiplexer_65 (.in0(2'b00), .in1(2'b00), .out(A1op11), .sel(and_5_out));
  Multiplexer #(.enable("false")) multiplexer_66 (.in0(1'b0), .in1(1'b0), .out(A2op11), .sel(and_5_out));
  Multiplexer #(.width(2), .enable("false")) multiplexer_67 (.in0(2'b00), .in1(2'b00), .out(A3op11), .sel(and_5_out));
  Multiplexer #(.width(2), .enable("false")) multiplexer_68 (.in0(2'b00), .in1(2'b00), .out(REGop11), .sel(and_5_out));
  Multiplexer #(.enable("false")) multiplexer_69 (.in0(1'b0), .in1(1'b1), .out(RegWrite11), .sel(and_5_out));
  Multiplexer #(.enable("false")) multiplexer_70 (.in0(1'b0), .in1(1'b0), .out(ALU_Aop11), .sel(and_5_out));
  Multiplexer #(.width(2), .enable("false")) multiplexer_71 (
    .in0(2'b00), .in1(2'b00), .out(ALU_Bop11), .sel(and_5_out));
  Multiplexer #(.width(4), .enable("false")) multiplexer_72 (
    .in0(4'b0000), .in1(4'b0111), .out(ALUOp11), .sel(and_5_out));
  // Probe on 4'b0111
  // Probe on 6'b100011
  // Probe on 6'b000010
  Comparator #(.width(6), .mode("unsigned")) comparator_12 (
    .a(opcode), .b(6'b100011), .eq(comparator_12_eq));  // open: gt, lt
  Comparator #(.width(6), .mode("unsigned")) comparator_13 (
    .a(opcode), .b(6'b000010), .eq(comparator_13_eq));  // open: gt, lt
  Multiplexer #(.enable("false")) multiplexer_73 (.in0(1'b0), .in1(1'b1), .out(REGorMEM4), .sel(comparator_12_eq));
  Multiplexer #(.enable("false")) multiplexer_74 (.in0(1'b0), .in1(1'b0), .out(MemWrite4), .sel(comparator_12_eq));
  Multiplexer #(.width(3), .enable("false")) multiplexer_75 (
    .in0(3'b000), .in1(3'b000), .out(NPCop4), .sel(comparator_12_eq));
  Multiplexer #(.enable("false")) multiplexer_76 (.in0(1'b0), .in1(1'b0), .out(ZeroEXT4), .sel(comparator_12_eq));
  Multiplexer #(.width(2), .enable("false")) multiplexer_77 (
    .in0(2'b00), .in1(2'b00), .out(A1op4), .sel(comparator_12_eq));
  Multiplexer #(.enable("false")) multiplexer_78 (.in0(1'b0), .in1(1'b0), .out(A2op4), .sel(comparator_12_eq));
  Multiplexer #(.width(2), .enable("false")) multiplexer_79 (
    .in0(2'b00), .in1(2'b01), .out(A3op4), .sel(comparator_12_eq));
  Multiplexer #(.width(2), .enable("false")) multiplexer_80 (
    .in0(2'b00), .in1(2'b00), .out(REGop4), .sel(comparator_12_eq));
  Multiplexer #(.enable("false")) multiplexer_81 (.in0(1'b0), .in1(1'b1), .out(RegWrite4), .sel(comparator_12_eq));
  Multiplexer #(.enable("false")) multiplexer_82 (.in0(1'b0), .in1(1'b0), .out(ALU_Aop4), .sel(comparator_12_eq));
  Multiplexer #(.width(2), .enable("false")) multiplexer_83 (
    .in0(2'b00), .in1(2'b01), .out(ALU_Bop4), .sel(comparator_12_eq));
  Multiplexer #(.width(4), .enable("false")) multiplexer_84 (
    .in0(4'b0000), .in1(4'b0010), .out(ALUOp4), .sel(comparator_12_eq));
  // Probe on 4'b0010
  // Probe on 4'b0000
  Multiplexer #(.enable("false")) multiplexer_85 (.in0(1'b0), .in1(1'b0), .out(REGorMEM12), .sel(comparator_13_eq));
  Multiplexer #(.enable("false")) multiplexer_86 (.in0(1'b0), .in1(1'b0), .out(MemWrite12), .sel(comparator_13_eq));
  Multiplexer #(.width(3), .enable("false")) multiplexer_87 (
    .in0(3'b000), .in1(3'b010), .out(NPCop12), .sel(comparator_13_eq));
  Multiplexer #(.enable("false")) multiplexer_88 (.in0(1'b0), .in1(1'b0), .out(ZeroEXT12), .sel(comparator_13_eq));
  Multiplexer #(.width(2), .enable("false")) multiplexer_89 (
    .in0(2'b00), .in1(2'b00), .out(A1op12), .sel(comparator_13_eq));
  Multiplexer #(.enable("false")) multiplexer_90 (.in0(1'b0), .in1(1'b0), .out(A2op12), .sel(comparator_13_eq));
  Multiplexer #(.width(2), .enable("false")) multiplexer_91 (
    .in0(2'b00), .in1(2'b00), .out(A3op12), .sel(comparator_13_eq));
  Multiplexer #(.width(2), .enable("false")) multiplexer_92 (
    .in0(2'b00), .in1(2'b00), .out(REGop12), .sel(comparator_13_eq));
  Multiplexer #(.enable("false")) multiplexer_93 (.in0(1'b0), .in1(1'b0), .out(RegWrite12), .sel(comparator_13_eq));
  Multiplexer #(.enable("false")) multiplexer_94 (.in0(1'b0), .in1(1'b0), .out(ALU_Aop12), .sel(comparator_13_eq));
  Multiplexer #(.width(2), .enable("false")) multiplexer_95 (
    .in0(2'b00), .in1(2'b00), .out(ALU_Bop12), .sel(comparator_13_eq));
  Multiplexer #(.width(4), .enable("false")) multiplexer_96 (
    .in0(4'b0000), .in1(4'b0000), .out(ALUOp12), .sel(comparator_13_eq));
  // Probe on 6'b101011
  // Probe on 6'b000011
  Comparator #(.width(6), .mode("unsigned")) comparator_14 (
    .a(opcode), .b(6'b101011), .eq(comparator_14_eq));  // open: gt, lt
  Comparator #(.width(6), .mode("unsigned")) comparator_15 (
    .a(opcode), .b(6'b000011), .eq(comparator_15_eq));  // open: gt, lt
  Multiplexer #(.enable("false")) multiplexer_97 (.in0(1'b0), .in1(1'b0), .out(REGorMEM5), .sel(comparator_14_eq));
  Multiplexer #(.enable("false")) multiplexer_98 (.in0(1'b0), .in1(1'b1), .out(MemWrite5), .sel(comparator_14_eq));
  Multiplexer #(.width(3), .enable("false")) multiplexer_99 (
    .in0(3'b000), .in1(3'b000), .out(NPCop5), .sel(comparator_14_eq));
  Multiplexer #(.enable("false")) multiplexer_100 (.in0(1'b0), .in1(1'b0), .out(ZeroEXT5), .sel(comparator_14_eq));
  Multiplexer #(.width(2), .enable("false")) multiplexer_101 (
    .in0(2'b00), .in1(2'b00), .out(A1op5), .sel(comparator_14_eq));
  Multiplexer #(.enable("false")) multiplexer_102 (.in0(1'b0), .in1(1'b0), .out(A2op5), .sel(comparator_14_eq));
  Multiplexer #(.width(2), .enable("false")) multiplexer_103 (
    .in0(2'b00), .in1(2'b00), .out(A3op5), .sel(comparator_14_eq));
  Multiplexer #(.width(2), .enable("false")) multiplexer_104 (
    .in0(2'b00), .in1(2'b00), .out(REGop5), .sel(comparator_14_eq));
  Multiplexer #(.enable("false")) multiplexer_105 (.in0(1'b0), .in1(1'b0), .out(RegWrite5), .sel(comparator_14_eq));
  Multiplexer #(.enable("false")) multiplexer_106 (.in0(1'b0), .in1(1'b0), .out(ALU_Aop5), .sel(comparator_14_eq));
  Multiplexer #(.width(2), .enable("false")) multiplexer_107 (
    .in0(2'b00), .in1(2'b01), .out(ALU_Bop5), .sel(comparator_14_eq));
  Multiplexer #(.width(4), .enable("false")) multiplexer_108 (
    .in0(4'b0000), .in1(4'b0010), .out(ALUOp5), .sel(comparator_14_eq));
  // Probe on 4'b0010
  Multiplexer #(.enable("false")) multiplexer_109 (.in0(1'b0), .in1(1'b0), .out(REGorMEM13), .sel(comparator_15_eq));
  Multiplexer #(.enable("false")) multiplexer_110 (.in0(1'b0), .in1(1'b0), .out(MemWrite13), .sel(comparator_15_eq));
  Multiplexer #(.width(3), .enable("false")) multiplexer_111 (
    .in0(3'b000), .in1(3'b010), .out(NPCop13), .sel(comparator_15_eq));
  Multiplexer #(.enable("false")) multiplexer_112 (.in0(1'b0), .in1(1'b0), .out(ZeroEXT13), .sel(comparator_15_eq));
  Multiplexer #(.width(2), .enable("false")) multiplexer_113 (
    .in0(2'b00), .in1(2'b00), .out(A1op13), .sel(comparator_15_eq));
  Multiplexer #(.enable("false")) multiplexer_114 (.in0(1'b0), .in1(1'b0), .out(A2op13), .sel(comparator_15_eq));
  Multiplexer #(.width(2), .enable("false")) multiplexer_115 (
    .in0(2'b00), .in1(2'b10), .out(A3op13), .sel(comparator_15_eq));
  Multiplexer #(.width(2), .enable("false")) multiplexer_116 (
    .in0(2'b00), .in1(2'b10), .out(REGop13), .sel(comparator_15_eq));
  Multiplexer #(.enable("false")) multiplexer_117 (.in0(1'b0), .in1(1'b1), .out(RegWrite13), .sel(comparator_15_eq));
  Multiplexer #(.enable("false")) multiplexer_118 (.in0(1'b0), .in1(1'b0), .out(ALU_Aop13), .sel(comparator_15_eq));
  Multiplexer #(.width(2), .enable("false")) multiplexer_119 (
    .in0(2'b00), .in1(2'b00), .out(ALU_Bop13), .sel(comparator_15_eq));
  Multiplexer #(.width(4), .enable("false")) multiplexer_120 (
    .in0(4'b0000), .in1(4'b0000), .out(ALUOp13), .sel(comparator_15_eq));
  // Probe on 4'b0000
  // Probe on 6'b001001
  // Probe on {6{1'b0}}
  Comparator #(.width(6), .mode("unsigned")) comparator_16 (
    .a(funct), .b(6'b001001), .eq(comparator_16_eq));  // open: gt, lt
  Comparator #(.width(6), .mode("unsigned")) comparator_17 (
    .a(opcode), .b({6{1'b0}}), .eq(comparator_17_eq));  // open: gt, lt
  // Probe on 6'b000100
  and and_6 (and_6_out, comparator_16_eq, comparator_17_eq);
  Comparator #(.width(6), .mode("unsigned")) comparator_18 (
    .a(opcode), .b(6'b000100), .eq(comparator_18_eq));  // open: gt, lt
  // Probe on 4'b0000
  Multiplexer #(.enable("false")) multiplexer_121 (.in0(1'b0), .in1(1'b0), .out(REGorMEM6), .sel(comparator_18_eq));
  Multiplexer #(.enable("false")) multiplexer_122 (.in0(1'b0), .in1(1'b0), .out(MemWrite6), .sel(comparator_18_eq));
  Multiplexer #(.width(3), .enable("false")) multiplexer_123 (
    .in0(3'b000), .in1(3'b001), .out(NPCop6), .sel(comparator_18_eq));
  Multiplexer #(.enable("false")) multiplexer_124 (.in0(1'b0), .in1(1'b0), .out(ZeroEXT6), .sel(comparator_18_eq));
  Multiplexer #(.width(2), .enable("false")) multiplexer_125 (
    .in0(2'b00), .in1(2'b00), .out(A1op6), .sel(comparator_18_eq));
  Multiplexer #(.enable("false")) multiplexer_126 (.in0(1'b0), .in1(1'b0), .out(A2op6), .sel(comparator_18_eq));
  Multiplexer #(.width(2), .enable("false")) multiplexer_127 (
    .in0(2'b00), .in1(2'b00), .out(A3op6), .sel(comparator_18_eq));
  Multiplexer #(.width(2), .enable("false")) multiplexer_128 (
    .in0(2'b00), .in1(2'b00), .out(REGop6), .sel(comparator_18_eq));
  Multiplexer #(.enable("false")) multiplexer_129 (.in0(1'b0), .in1(1'b0), .out(RegWrite6), .sel(comparator_18_eq));
  Multiplexer #(.enable("false")) multiplexer_130 (.in0(1'b0), .in1(1'b0), .out(ALU_Aop6), .sel(comparator_18_eq));
  Multiplexer #(.width(2), .enable("false")) multiplexer_131 (
    .in0(2'b00), .in1(2'b00), .out(ALU_Bop6), .sel(comparator_18_eq));
  Multiplexer #(.width(4), .enable("false")) multiplexer_132 (
    .in0(4'b0000), .in1(4'b0000), .out(ALUOp6), .sel(comparator_18_eq));
  // Probe on 4'b0000
  Multiplexer #(.enable("false")) multiplexer_133 (.in0(1'b0), .in1(1'b0), .out(REGorMEM14), .sel(and_6_out));
  Multiplexer #(.enable("false")) multiplexer_134 (.in0(1'b0), .in1(1'b0), .out(MemWrite14), .sel(and_6_out));
  Multiplexer #(.width(3), .enable("false")) multiplexer_135 (
    .in0(3'b000), .in1(3'b011), .out(NPCop14), .sel(and_6_out));
  Multiplexer #(.enable("false")) multiplexer_136 (.in0(1'b0), .in1(1'b0), .out(ZeroEXT14), .sel(and_6_out));
  Multiplexer #(.width(2), .enable("false")) multiplexer_137 (.in0(2'b00), .in1(2'b00), .out(A1op14), .sel(and_6_out));
  Multiplexer #(.enable("false")) multiplexer_138 (.in0(1'b0), .in1(1'b0), .out(A2op14), .sel(and_6_out));
  Multiplexer #(.width(2), .enable("false")) multiplexer_139 (.in0(2'b00), .in1(2'b00), .out(A3op14), .sel(and_6_out));
  Multiplexer #(.width(2), .enable("false")) multiplexer_140 (.in0(2'b00), .in1(2'b10), .out(REGop14), .sel(and_6_out));
  Multiplexer #(.enable("false")) multiplexer_141 (.in0(1'b0), .in1(1'b1), .out(RegWrite14), .sel(and_6_out));
  Multiplexer #(.enable("false")) multiplexer_142 (.in0(1'b0), .in1(1'b0), .out(ALU_Aop14), .sel(and_6_out));
  Multiplexer #(.width(2), .enable("false")) multiplexer_143 (
    .in0(2'b00), .in1(2'b00), .out(ALU_Bop14), .sel(and_6_out));
  Multiplexer #(.width(4), .enable("false")) multiplexer_144 (
    .in0(4'b0000), .in1(4'b0000), .out(ALUOp14), .sel(and_6_out));
  // Probe on 6'b001000
  // Probe on {6{1'b0}}
  // Probe on 6'b001111
  Comparator #(.width(6), .mode("unsigned")) comparator_19 (
    .a(funct), .b(6'b001000), .eq(comparator_19_eq));  // open: gt, lt
  Comparator #(.width(6), .mode("unsigned")) comparator_20 (
    .a(opcode), .b({6{1'b0}}), .eq(comparator_20_eq));  // open: gt, lt
  Comparator #(.width(6), .mode("unsigned")) comparator_21 (
    .a(opcode), .b(6'b001111), .eq(comparator_21_eq));  // open: gt, lt
  and and_7 (and_7_out, comparator_19_eq, comparator_20_eq);
  Multiplexer #(.enable("false")) multiplexer_145 (.in0(1'b0), .in1(1'b0), .out(REGorMEM7), .sel(comparator_21_eq));
  Multiplexer #(.enable("false")) multiplexer_146 (.in0(1'b0), .in1(1'b0), .out(MemWrite7), .sel(comparator_21_eq));
  Multiplexer #(.width(3), .enable("false")) multiplexer_147 (
    .in0(3'b000), .in1(3'b000), .out(NPCop7), .sel(comparator_21_eq));
  Multiplexer #(.enable("false")) multiplexer_148 (.in0(1'b0), .in1(1'b0), .out(ZeroEXT7), .sel(comparator_21_eq));
  Multiplexer #(.width(2), .enable("false")) multiplexer_149 (
    .in0(2'b00), .in1(2'b00), .out(A1op7), .sel(comparator_21_eq));
  Multiplexer #(.enable("false")) multiplexer_150 (.in0(1'b0), .in1(1'b0), .out(A2op7), .sel(comparator_21_eq));
  Multiplexer #(.width(2), .enable("false")) multiplexer_151 (
    .in0(2'b00), .in1(2'b01), .out(A3op7), .sel(comparator_21_eq));
  Multiplexer #(.width(2), .enable("false")) multiplexer_152 (
    .in0(2'b00), .in1(2'b01), .out(REGop7), .sel(comparator_21_eq));
  Multiplexer #(.enable("false")) multiplexer_153 (.in0(1'b0), .in1(1'b1), .out(RegWrite7), .sel(comparator_21_eq));
  Multiplexer #(.enable("false")) multiplexer_154 (.in0(1'b0), .in1(1'b0), .out(ALU_Aop7), .sel(comparator_21_eq));
  Multiplexer #(.width(2), .enable("false")) multiplexer_155 (
    .in0(2'b00), .in1(2'b00), .out(ALU_Bop7), .sel(comparator_21_eq));
  Multiplexer #(.width(4), .enable("false")) multiplexer_156 (
    .in0(4'b0000), .in1(4'b0000), .out(ALUOp7), .sel(comparator_21_eq));
  // Probe on 4'b0000
  Multiplexer #(.enable("false")) multiplexer_157 (.in0(1'b0), .in1(1'b0), .out(REGorMEM15), .sel(and_7_out));
  Multiplexer #(.enable("false")) multiplexer_158 (.in0(1'b0), .in1(1'b0), .out(MemWrite15), .sel(and_7_out));
  Multiplexer #(.width(3), .enable("false")) multiplexer_159 (
    .in0(3'b000), .in1(3'b011), .out(NPCop15), .sel(and_7_out));
  Multiplexer #(.enable("false")) multiplexer_160 (.in0(1'b0), .in1(1'b0), .out(ZeroEXT15), .sel(and_7_out));
  Multiplexer #(.width(2), .enable("false")) multiplexer_161 (.in0(2'b00), .in1(2'b00), .out(A1op15), .sel(and_7_out));
  Multiplexer #(.enable("false")) multiplexer_162 (.in0(1'b0), .in1(1'b0), .out(A2op15), .sel(and_7_out));
  Multiplexer #(.width(2), .enable("false")) multiplexer_163 (.in0(2'b00), .in1(2'b00), .out(A3op15), .sel(and_7_out));
  Multiplexer #(.width(2), .enable("false")) multiplexer_164 (.in0(2'b00), .in1(2'b00), .out(REGop15), .sel(and_7_out));
  Multiplexer #(.enable("false")) multiplexer_165 (.in0(1'b0), .in1(1'b0), .out(RegWrite15), .sel(and_7_out));
  Multiplexer #(.enable("false")) multiplexer_166 (.in0(1'b0), .in1(1'b0), .out(ALU_Aop15), .sel(and_7_out));
  Multiplexer #(.width(2), .enable("false")) multiplexer_167 (
    .in0(2'b00), .in1(2'b00), .out(ALU_Bop15), .sel(and_7_out));
  Multiplexer #(.width(4), .enable("false")) multiplexer_168 (
    .in0(4'b0000), .in1(4'b0000), .out(ALUOp15), .sel(and_7_out));
  // Probe on 4'b0000
  // Probe on {6{1'b0}}
  // Probe on {6{1'b0}}
  // Probe on {6{1'b0}}
  // Probe on {6{1'b0}}
  Comparator #(.width(6), .mode("unsigned")) comparator_22 (
    .a(funct), .b({6{1'b0}}), .eq(comparator_22_eq));  // open: gt, lt
  Comparator #(.width(6), .mode("unsigned")) comparator_23 (
    .a(opcode), .b({6{1'b0}}), .eq(comparator_23_eq));  // open: gt, lt
  Comparator #(.width(6), .mode("unsigned")) comparator_24 (
    .a(funct), .b({6{1'b0}}), .eq(comparator_24_eq));  // open: gt, lt
  Comparator #(.width(6), .mode("unsigned")) comparator_25 (
    .a(opcode), .b({6{1'b0}}), .eq(comparator_25_eq));  // open: gt, lt
  and and_8 (and_8_out, comparator_22_eq, comparator_23_eq);
  and and_9 (and_9_out, comparator_24_eq, comparator_25_eq);
  Multiplexer #(.enable("false")) multiplexer_169 (.in0(1'b0), .in1(1'b0), .out(REGorMEM8), .sel(and_8_out));
  Multiplexer #(.enable("false")) multiplexer_170 (.in0(1'b0), .in1(1'b0), .out(MemWrite8), .sel(and_8_out));
  Multiplexer #(.width(3), .enable("false")) multiplexer_171 (
    .in0(3'b000), .in1(3'b000), .out(NPCop8), .sel(and_8_out));
  Multiplexer #(.enable("false")) multiplexer_172 (.in0(1'b0), .in1(1'b0), .out(ZeroEXT8), .sel(and_8_out));
  Multiplexer #(.width(2), .enable("false")) multiplexer_173 (.in0(2'b00), .in1(2'b01), .out(A1op8), .sel(and_8_out));
  Multiplexer #(.enable("false")) multiplexer_174 (.in0(1'b0), .in1(1'b0), .out(A2op8), .sel(and_8_out));
  Multiplexer #(.width(2), .enable("false")) multiplexer_175 (.in0(2'b00), .in1(2'b00), .out(A3op8), .sel(and_8_out));
  Multiplexer #(.width(2), .enable("false")) multiplexer_176 (.in0(2'b00), .in1(2'b00), .out(REGop8), .sel(and_8_out));
  Multiplexer #(.enable("false")) multiplexer_177 (.in0(1'b0), .in1(1'b1), .out(RegWrite8), .sel(and_8_out));
  Multiplexer #(.enable("false")) multiplexer_178 (.in0(1'b0), .in1(1'b0), .out(ALU_Aop8), .sel(and_8_out));
  Multiplexer #(.width(2), .enable("false")) multiplexer_179 (
    .in0(2'b00), .in1(2'b10), .out(ALU_Bop8), .sel(and_8_out));
  Multiplexer #(.width(4), .enable("false")) multiplexer_180 (
    .in0(4'b0000), .in1(4'b0100), .out(ALUOp8), .sel(and_8_out));
  // Probe on 4'b0100
  Multiplexer #(.enable("false")) multiplexer_181 (.in0(1'b0), .in1(1'b0), .out(REGorMEM16), .sel(undriven));
  Multiplexer #(.enable("false")) multiplexer_182 (.in0(1'b0), .in1(1'b0), .out(MemWrite16), .sel(undriven));
  Multiplexer #(.width(3), .enable("false")) multiplexer_183 (
    .in0(3'b000), .in1(3'b011), .out(NPCop16), .sel(undriven));
  Multiplexer #(.enable("false")) multiplexer_184 (.in0(1'b0), .in1(1'b0), .out(ZeroEXT16), .sel(undriven));
  Multiplexer #(.width(2), .enable("false")) multiplexer_185 (.in0(2'b00), .in1(2'b00), .out(A1op16), .sel(undriven));
  Multiplexer #(.enable("false")) multiplexer_186 (.in0(1'b0), .in1(1'b0), .out(A2op16), .sel(undriven));
  Multiplexer #(.width(2), .enable("false")) multiplexer_187 (.in0(2'b00), .in1(2'b00), .out(A3op16), .sel(undriven));
  Multiplexer #(.width(2), .enable("false")) multiplexer_188 (.in0(2'b00), .in1(2'b00), .out(REGop16), .sel(undriven));
  Multiplexer #(.enable("false")) multiplexer_189 (.in0(1'b0), .in1(1'b0), .out(RegWrite16), .sel(undriven));
  Multiplexer #(.enable("false")) multiplexer_190 (.in0(1'b0), .in1(1'b0), .out(ALU_Aop16), .sel(undriven));
  Multiplexer #(.width(2), .enable("false")) multiplexer_191 (
    .in0(2'b00), .in1(2'b00), .out(ALU_Bop16), .sel(undriven));
  Multiplexer #(.width(4), .enable("false")) multiplexer_192 (
    .in0(4'b0000), .in1(4'b0000), .out(ALUOp16), .sel(undriven));
  // Probe on 4'b0000
  or or_1 (REGorMEM, REGorMEM1, REGorMEM2, REGorMEM3, REGorMEM4, REGorMEM5, REGorMEM6, REGorMEM7, REGorMEM8, REGorMEM9, REGorMEM10, REGorMEM11, REGorMEM12, REGorMEM13, REGorMEM14, REGorMEM15);
  or or_2 (MemWrite, MemWrite1, MemWrite2, MemWrite3, MemWrite4, MemWrite5, MemWrite6, MemWrite7, MemWrite8, MemWrite9, MemWrite10, MemWrite11, MemWrite12, MemWrite13, MemWrite14, MemWrite15);
  assign NPCop = NPCop1 | NPCop2 | NPCop3 | NPCop4 | NPCop5 | NPCop6 | NPCop7 | NPCop8 | NPCop9 | NPCop10 | NPCop11 | NPCop12 | NPCop13 | NPCop14 | NPCop15;  // OR_Gate or_3, 3 bits wide
  or or_4 (ZeroEXT, ZeroEXT1, ZeroEXT2, ZeroEXT3, ZeroEXT4, ZeroEXT5, ZeroEXT6, ZeroEXT7, ZeroEXT8, ZeroEXT9, ZeroEXT10, ZeroEXT11, ZeroEXT12, ZeroEXT13, ZeroEXT14, ZeroEXT15);
  assign A1op = A1op1 | A1op2 | A1op3 | A1op4 | A1op5 | A1op6 | A1op7 | A1op8 | A1op9 | A1op10 | A1op11 | A1op12 | A1op13 | A1op14 | A1op15;  // OR_Gate or_5, 2 bits wide
  or or_6 (A2op, A2op1, A2op2, A2op3, A2op4, A2op5, A2op6, A2op7, A2op8, A2op9, A2op10, A2op11, A2op12, A2op13, A2op14, A2op15);
  assign A3op = A3op1 | A3op2 | A3op3 | A3op4 | A3op5 | A3op6 | A3op7 | A3op8 | A3op9 | A3op10 | A3op11 | A3op12 | A3op13 | A3op14 | A3op15;  // OR_Gate or_7, 2 bits wide
  assign REGop = REGop1 | REGop2 | REGop3 | REGop4 | REGop5 | REGop6 | REGop7 | REGop8 | REGop9 | REGop10 | REGop11 | REGop12 | REGop13 | REGop14 | REGop15;  // OR_Gate or_8, 2 bits wide
  or or_9 (RegWrite, RegWrite1, RegWrite2, RegWrite3, RegWrite4, RegWrite5, RegWrite6, RegWrite7, RegWrite8, RegWrite9, RegWrite10, RegWrite11, RegWrite12, RegWrite13, RegWrite14, RegWrite15);
  or or_10 (ALU_Aop, ALU_Aop1, ALU_Aop2, ALU_Aop3, ALU_Aop4, ALU_Aop5, ALU_Aop6, ALU_Aop7, ALU_Aop8, ALU_Aop9, ALU_Aop10, ALU_Aop11, ALU_Aop12, ALU_Aop13, ALU_Aop14, ALU_Aop15);
  assign ALU_Bop = ALU_Bop1 | ALU_Bop2 | ALU_Bop3 | ALU_Bop4 | ALU_Bop5 | ALU_Bop6 | ALU_Bop7 | ALU_Bop8 | ALU_Bop9 | ALU_Bop10 | ALU_Bop11 | ALU_Bop12 | ALU_Bop13 | ALU_Bop14 | ALU_Bop15;  // OR_Gate or_11, 2 bits wide
  assign ALUOp = ALUOp1 | ALUOp2 | ALUOp3 | ALUOp4 | ALUOp5 | ALUOp6 | ALUOp7 | ALUOp8 | ALUOp9 | ALUOp10 | ALUOp11 | ALUOp12 | ALUOp13 | ALUOp14 | ALUOp15;  // OR_Gate or_12, 4 bits wide

  // Notes on the sheet:
  //   ADDU
  //   SRL
  //   SUBU
  //   SRA
  //   ORI
  //   SLT
  //   LW
  //   J
  //   SW
  //   JAL
  //   JALR
  //   BEQ
  //   LUI
  //   JR
  //   NEW!!!!
  //   SLL
endmodule

module new_pc (
  input  [31:0] NPC,
  input  CLK,
  input  RESET,
  output [31:0] PC
);

  wire comparator_1_eq, or_1_out;
  wire [31:0] register_1_q;

  Register #(.width(32)) register_1 (.D(NPC), .Q(register_1_q), .clk(CLK), .clr(RESET));  // open: en
  Comparator #(.width(32)) comparator_1 (.a(register_1_q), .b({32{1'b0}}), .eq(comparator_1_eq));  // open: gt, lt
  Multiplexer #(.width(32), .enable("false")) multiplexer_1 (
    .in0(register_1_q), .in1(32'h3000), .out(PC), .sel(or_1_out));
  or or_1 (or_1_out, comparator_1_eq, RESET);
endmodule
