// Logisim project datapath.circ as structural Verilog: 17 circuits, main circuit main
module main (
);

  wire cmp_1_zero, d_decoder_1_extop, e_decoder_1_alu_aop, m_decoder_1_memwrite_m, RegWrite_W,
       w_decoder_1_regormem_w;
  wire [1:0] e_decoder_1_alu_bop, w_decoder_1_regop_w;
  wire [2:0] d_decoder_1_npcop, MF_ALUA_E_sel, MF_ALUB_E_sel, MF_GRFRD1_D_sel, MF_GRFRD2_D_sel;
  wire [3:0] e_decoder_1_aluop;
  wire [4:0] A3_W, d_decoder_1_a1_d, d_decoder_1_a2_d, e_decoder_1_shamt_e;
  wire [31:0] alu_1_aluresult_e, ALUResult_M, ALUResult_W, dm_1_dm_rd, DM_RD_W, ext_1_extresult, grf_1_rd1,
       grf_1_rd2, im_1_ir, multiplexer_1_out, multiplexer_2_out, multiplexer_3_out, multiplexer_4_out,
       multiplexer_5_out, multiplexer_6_out, multiplexer_7_out, multiplexer_8_out, multiplexer_9_out,
       npc_1_npc, pc4_M, pc4_W, pc_1_pc4_f, pc_1_pc8_f, pc_1_pc_f, reg_d_1_ir_d, reg_d_1_pc4_d,
       reg_d_1_pc8_d, reg_e_1_extresult_e, reg_e_1_ir_e, reg_e_1_pc4_e, reg_e_1_pc8_e, reg_e_1_v1_e,
       reg_e_1_v2_e, reg_m_1_aluresult_m, reg_m_1_ir_m, reg_m_1_pc4_m, reg_m_1_pc8_m, reg_m_1_v2_m,
       reg_w_1_aluresult_w, reg_w_1_dm_rd_w, reg_w_1_ir_w, reg_w_1_pc8_w, RegData_W, undriven, undriven_2;

  PC pc_1 (.NPC(npc_1_npc), .PC_F(pc_1_pc_f), .PC8_F(pc_1_pc8_f), .PC4_F(pc_1_pc4_f));  // open: clk, pc_en, reset
  IM im_1 (.PC(pc_1_pc_f), .IR(im_1_ir));
  REG_D reg_d_1 (
    .IR_F(im_1_ir), .pc4_F(pc_1_pc8_f), .pc8_F(pc_1_pc4_f), .IR_D(reg_d_1_ir_d), .pc4_D(reg_d_1_pc4_d),
    .pc8_D(reg_d_1_pc8_d));  // open: clk, reset, D_en
  D_DECODER d_decoder_1 (
    .IR_D(reg_d_1_ir_d), .A1_D(d_decoder_1_a1_d), .A2_D(d_decoder_1_a2_d), .EXTOp(d_decoder_1_extop),
    .NPCOp(d_decoder_1_npcop));
  NPC npc_1 (
    .IR_D(reg_d_1_ir_d), .NPCOp(d_decoder_1_npcop), .pc4_D(reg_d_1_pc4_d), .pc8_D(reg_d_1_pc8_d),
    .GPR_rs(multiplexer_1_out), .zero(cmp_1_zero), .npc(npc_1_npc));
  EXT ext_1 (.IR_D(reg_d_1_ir_d), .EXTOp(d_decoder_1_extop), .EXTResult(ext_1_extresult));
  GRF grf_1 (
    .pc4_D(reg_d_1_pc4_d), .pc8_D(reg_d_1_pc8_d), .A1_D(d_decoder_1_a1_d), .A2_D(d_decoder_1_a2_d),
    .A3_W(A3_W), .RegData(RegData_W), .RD1(grf_1_rd1), .RD2(grf_1_rd2), .RegWrite_W(RegWrite_W));  // open: clk, reset
  Multiplexer #(.select(3), .width(32), .enable("false")) multiplexer_1 (
    .in0(grf_1_rd1), .in1(ALUResult_M), .in2(pc4_M), .in3(ALUResult_W), .in4(DM_RD_W), .in5(pc4_W),
    .out(multiplexer_1_out), .sel(MF_GRFRD1_D_sel));  // open: in6, in7
  Multiplexer #(.select(3), .width(32), .enable("false")) multiplexer_2 (
    .in0(grf_1_rd2), .in1(ALUResult_M), .in2(pc4_M), .in3(ALUResult_W), .in4(DM_RD_W), .in5(pc4_W),
    .out(multiplexer_2_out), .sel(MF_GRFRD2_D_sel));  // open: in6, in7
  CMP cmp_1 (.V1(multiplexer_1_out), .V2(multiplexer_2_out), .zero(cmp_1_zero));
  E_DECODER e_decoder_1 (
    .IR_E(reg_e_1_ir_e), .ALU_Aop(e_decoder_1_alu_aop), .ALU_Bop(e_decoder_1_alu_bop),
    .ALUOp(e_decoder_1_aluop), .shamt_E(e_decoder_1_shamt_e));
  REG_E reg_e_1 (
    .IR_D(reg_d_1_ir_d), .V1(multiplexer_1_out), .V2(multiplexer_2_out), .EXTResult(ext_1_extresult),
    .pc4_D(reg_d_1_pc4_d), .pc8_D(reg_d_1_pc8_d), .IR_E(reg_e_1_ir_e), .V1_E(reg_e_1_v1_e),
    .V2_E(reg_e_1_v2_e), .EXTResult_E(reg_e_1_extresult_e), .pc4_E(reg_e_1_pc4_e), .pc8_E(reg_e_1_pc8_e));  // open: clk, reset, E_clr
  Multiplexer #(.select(3), .width(32), .enable("false")) multiplexer_3 (
    .in0(reg_e_1_v1_e), .in1(ALUResult_M), .in2(pc4_M), .in3(ALUResult_W), .in4(DM_RD_W), .in5(pc4_W),
    .out(multiplexer_3_out), .sel(MF_ALUA_E_sel));  // open: in6, in7
  Multiplexer #(.select(3), .width(32), .enable("false")) multiplexer_4 (
    .in0(reg_e_1_v2_e), .in1(ALUResult_M), .in2(pc4_M), .in3(ALUResult_W), .in4(DM_RD_W), .in5(pc4_W),
    .out(multiplexer_4_out), .sel(MF_ALUB_E_sel));  // open: in6, in7
  Multiplexer #(.width(32), .enable("false")) multiplexer_5 (
    .in0(multiplexer_3_out), .out(multiplexer_5_out), .sel(e_decoder_1_alu_aop));  // open: in1
  Multiplexer #(.select(2), .width(32), .enable("false")) multiplexer_6 (
    .in0(multiplexer_4_out), .in1(reg_e_1_extresult_e), .out(multiplexer_6_out), .sel(e_decoder_1_alu_bop));  // open: in2, in3
  Multiplexer #(.select(3), .width(32), .enable("false")) multiplexer_7 (
    .in0(reg_e_1_v2_e), .in1(ALUResult_M), .in2(pc4_M), .in3(ALUResult_W), .in4(DM_RD_W), .in5(pc4_W),
    .out(multiplexer_7_out), .sel(MF_ALUB_E_sel));  // open: in6, in7
  ALU alu_1 (
    .ALUSrcA(multiplexer_5_out), .ALUSrcB(multiplexer_6_out), .ALUOp(e_decoder_1_aluop),
    .shamt_E(e_decoder_1_shamt_e), .ALUResult_E(alu_1_aluresult_e));
  REG_M reg_m_1 (
    .IR_E(reg_e_1_ir_e), .V2_E(multiplexer_7_out), .ALUResult_E(alu_1_aluresult_e), .pc4_E(reg_e_1_pc4_e),
    .pc8_E(reg_e_1_pc8_e), .IR_M(reg_m_1_ir_m), .V2_M(reg_m_1_v2_m), .ALUResult_M(reg_m_1_aluresult_m),
    .pc4_M(reg_m_1_pc4_m), .pc8_M(reg_m_1_pc8_m));  // open: clk, reset
  M_DECODER m_decoder_1 (.IR_M(reg_m_1_ir_m), .MemWrite_M(m_decoder_1_memwrite_m));
  Multiplexer #(.select(2), .width(32), .enable("false")) multiplexer_8 (
    .in0(reg_m_1_v2_m), .in1(ALUResult_W), .in2(DM_RD_W), .in3(pc4_W), .out(multiplexer_8_out));  // open: sel
  DM dm_1 (
    .pc4_M(reg_m_1_pc4_m), .MemAddr(reg_m_1_aluresult_m), .MemData(multiplexer_8_out),
    .MemWrite_M(m_decoder_1_memwrite_m), .DM_RD(dm_1_dm_rd));  // open: clk, reset
  REG_W reg_w_1 (
    .IR_M(reg_m_1_ir_m), .ALUResult_M(reg_m_1_aluresult_m), .pc4_M(reg_m_1_pc4_m), .pc8_M(reg_m_1_pc8_m),
    .DM_RD(dm_1_dm_rd), .IR_W(reg_w_1_ir_w), .ALUResult_W(reg_w_1_aluresult_w), .pc8_W(reg_w_1_pc8_w),
    .DM_RD_W(reg_w_1_dm_rd_w));  // open: pc4_W, clk, reset
  W_DECODER w_decoder_1 (
    .IR_W(reg_w_1_ir_w), .A3_W(A3_W), .RegWrite_W(RegWrite_W), .REGorMEM_W(w_decoder_1_regormem_w),
    .REGop_W(w_decoder_1_regop_w));
  Multiplexer #(.width(32), .enable("false")) multiplexer_9 (
    .in0(reg_w_1_aluresult_w), .in1(reg_w_1_dm_rd_w), .out(multiplexer_9_out), .sel(w_decoder_1_regormem_w));
  Multiplexer #(.select(2), .width(32), .disabled(0), .enable("false")) multiplexer_10 (
    .in0(multiplexer_9_out), .in1(undriven), .in2(reg_w_1_pc8_w), .in3(undriven_2), .out(RegData_W),
    .sel(w_decoder_1_regop_w));

  // Notes on the sheet:
  //   pc_F
  //   pc4_F
  //   npc
  //   pc8_F
  //   IR_F
  //   IR_D
  //   pc4_D
  //   pc8_D
  //   A1_D
  //   A2_D
  //   NPCOp
  //   EXTOp
  //   RD1
  //   RD2
  //   EXTResult
  //   MF_GRFRD1_D
  //   V1
  //   MF_GRFRD2_D
  //   V2
  //   zero
  //   IR_E
  //   EXTResult_E
  //   ALU_Aop
  //   ALU_Bop
  //   ALUOp
  //   shamt_E
  //   V1_E_left
  //   V2_E_left
  //   MF_ALUA_E
  //   MF_ALUB_E
  //   V1_E_right
  //   MUX_ALUSrcB
  //   V2_E_right_ALUB
  //   MUX_ALUSrcA
  //   ALUSrcA
  //   ALUSrcB
  //   V2_E_left
  //   pc4_E
  //   pc8_E
  //   MF_MemData_E
  //   ALUResult_E
  //   V2_E_right2_RegM
  //   IR_M
  //   MemWrite_W
  //   pc4_M
  //   V2_M
  //   ALUResult_M
  //   pc8_M
  //   MF_DMWD_M
  //   MemData
  //   DM_RD
  //   IR_W
  //   ALUResult_W
  //   DM_RD_W
  //   REGorMEM_W
  //   MUX_REGorMEM_Result
  //   REGorMEM_Result_W
  //   pc8_W
  //   REGop_W
  //   MUX_RegData
endmodule

module PC (
  input  [31:0] NPC,
  input  clk,
  input  pc_en,
  input  reset,
  output [31:0] PC_F,
  output [31:0] PC8_F,
  output [31:0] PC4_F
);
endmodule

module IM (
  input  [31:0] PC,
  output [31:0] IR
);
endmodule

module REG_D (
  input  clk,
  input  reset,
  input  D_en,
  input  [31:0] IR_F,
  input  [31:0] pc4_F,
  input  [31:0] pc8_F,
  output [31:0] IR_D,
  output [31:0] pc4_D,
  output [31:0] pc8_D
);
endmodule

module D_DECODER (
  input  [31:0] IR_D,
  output [4:0] A1_D,
  output [4:0] A2_D,
  output EXTOp,
  output [2:0] NPCOp
);
endmodule

module GRF (
  input  RegWrite_W,
  input  [31:0] pc4_D,
  input  [31:0] pc8_D,
  input  [4:0] A1_D,
  input  [4:0] A2_D,
  input  [4:0] A3_W,
  input  [31:0] RegData,
  input  clk,
  input  reset,
  output [31:0] RD1,
  output [31:0] RD2
);
endmodule

module CMP (
  input  [31:0] V1,
  input  [31:0] V2,
  output zero
);
endmodule

module EXT (
  input  [31:0] IR_D,
  input  EXTOp,
  output [31:0] EXTResult
);
endmodule

module NPC (
  input  [31:0] IR_D,
  input  [31:0] GPR_rs,
  input  [2:0] NPCOp,
  input  zero,
  input  [31:0] pc4_D,
  input  [31:0] pc8_D,
  output [31:0] npc
);
endmodule

module REG_E (
  input  [31:0] IR_D,
  input  [31:0] V1,
  input  [31:0] V2,
  input  [31:0] EXTResult,
  input  [31:0] pc4_D,
  input  [31:0] pc8_D,
  input  clk,
  input  reset,
  input  E_clr,
  output [31:0] IR_E,
  output [31:0] V1_E,
  output [31:0] V2_E,
  output [31:0] EXTResult_E,
  output [31:0] pc4_E,
  output [31:0] pc8_E
);
endmodule

module E_DECODER (
  input  [31:0] IR_E,
  output ALU_Aop,
  output [1:0] ALU_Bop,
  output [3:0] ALUOp,
  output [4:0] shamt_E
);
endmodule

module ALU (
  input  [31:0] ALUSrcA,
  input  [31:0] ALUSrcB,
  input  [3:0] ALUOp,
  input  [4:0] shamt_E,
  output [31:0] ALUResult_E
);
endmodule

module REG_M (
  input  [31:0] IR_E,
  input  [31:0] V2_E,
  input  [31:0] ALUResult_E,
  input  [31:0] pc4_E,
  input  [31:0] pc8_E,
  input  clk,
  input  reset,
  output [31:0] IR_M,
  output [31:0] V2_M,
  output [31:0] ALUResult_M,
  output [31:0] pc4_M,
  output [31:0] pc8_M
);
endmodule

module M_DECODER (
  input  [31:0] IR_M,
  output MemWrite_M
);
endmodule

module DM (
  input  [31:0] pc4_M,
  input  [31:0] MemAddr,
  input  [31:0] MemData,
  input  MemWrite_M,
  input  clk,
  input  reset,
  output [31:0] DM_RD
);
endmodule

module REG_W (
  input  [31:0] IR_M,
  input  [31:0] ALUResult_M,
  input  [31:0] pc4_M,
  input  [31:0] pc8_M,
  input  [31:0] DM_RD,
  input  clk,
  input  reset,
  output [31:0] IR_W,
  output [31:0] ALUResult_W,
  output [31:0] pc4_W,
  output [31:0] pc8_W,
  output [31:0] DM_RD_W
);
endmodule

module W_DECODER (
  input  [31:0] IR_W,
  output [4:0] A3_W,
  output RegWrite_W,
  output REGorMEM_W,
  output [1:0] REGop_W
);
endmodule
